// Logisim project 第1次实验.circ as structural Verilog: 9 circuits, main circuit LED计数测试
// LED计数
module \LED计数电路  (
  input  In1,
  input  In2,
  input  In3,
  input  In4,
  input  In5,
  output Out1,
  output Out1_2,
  output Out1_3,
  output Out1_4,
  output Out1_5
);

  or or_1 (Out1, In1, In2, In3, In4, In5);
  or or_2 (Out1_2, In2, In3, In4, In5);
  or or_3 (Out1_3, In3, In4, In5);
  or or_4 (Out1_4, In4, In5);

  assign Out1_5 = In5;
endmodule

module \LED计数测试  (
);

  wire _1_out, _2_out, _3_out, _4_out, _5_out, \led计数电路_1_out1 , \led计数电路_1_out1_2 , \led计数电路_1_out1_3 ,
       \led计数电路_1_out1_4 , \led计数电路_1_out1_5 , \n7段数码管显示驱动_1_seg_1 , \n7段数码管显示驱动_1_seg_2 ,
       \n7段数码管显示驱动_1_seg_3 , \n7段数码管显示驱动_1_seg_4 , \n7段数码管显示驱动_1_seg_5 , \n7段数码管显示驱动_1_seg_6 ,
       \n7段数码管显示驱动_1_seg_7 ;
  wire [2:0] \n5输入按键编码器设计_1_out1 ;

  Button _1 (.out(_1_out));
  Button _2 (.out(_2_out));
  Button _3 (.out(_3_out));
  Button _4 (.out(_4_out));
  Button _5 (.out(_5_out));
  \LED计数电路  \led计数电路_1  (
    .In1(_1_out), .In2(_2_out), .In3(_3_out), .In4(_4_out), .In5(_5_out), .Out1(\led计数电路_1_out1 ),
    .Out1_2(\led计数电路_1_out1_2 ), .Out1_3(\led计数电路_1_out1_3 ), .Out1_4(\led计数电路_1_out1_4 ),
    .Out1_5(\led计数电路_1_out1_5 ));
  \_5输入按键编码器设计  \u_5输入按键编码器设计_1  (
    .In1(_1_out), .In2(_2_out), .In3(_3_out), .In4(_4_out), .In5(_5_out), .Out1(\n5输入按键编码器设计_1_out1 [0]),
    .Out2(\n5输入按键编码器设计_1_out1 [1]), .Out3(\n5输入按键编码器设计_1_out1 [2]));
  LED #(.active("true")) led_1 (.in(\led计数电路_1_out1 ));
  LED #(.active("true")) led_2 (.in(\led计数电路_1_out1_2 ));
  LED #(.active("true")) led_3 (.in(\led计数电路_1_out1_3 ));
  LED #(.active("true")) led_4 (.in(\led计数电路_1_out1_4 ));
  LED #(.active("true")) led_5 (.in(\led计数电路_1_out1_5 ));
  // Probe on \n5输入按键编码器设计_1_out1 
  Hex_Digit_Display hex_digit_display_1 (.value({1'b0, \n5输入按键编码器设计_1_out1 }), .dp(1'b1));
  \_7段数码管显示驱动  \u_7段数码管显示驱动_1  (
    .X0(1'b0), .X1(\n5输入按键编码器设计_1_out1 [2]), .X2(\n5输入按键编码器设计_1_out1 [1]), .X3(\n5输入按键编码器设计_1_out1 [0]),
    .Seg_1(\n7段数码管显示驱动_1_seg_1 ), .Seg_2(\n7段数码管显示驱动_1_seg_2 ), .Seg_3(\n7段数码管显示驱动_1_seg_3 ),
    .Seg_4(\n7段数码管显示驱动_1_seg_4 ), .Seg_5(\n7段数码管显示驱动_1_seg_5 ), .Seg_6(\n7段数码管显示驱动_1_seg_6 ),
    .Seg_7(\n7段数码管显示驱动_1_seg_7 ));
  _7_Segment_Display #(.active("true")) u_7_segment_display_1 (
    .g(\n7段数码管显示驱动_1_seg_1 ), .f(\n7段数码管显示驱动_1_seg_2 ), .a(\n7段数码管显示驱动_1_seg_3 ), .b(\n7段数码管显示驱动_1_seg_4 ),
    .e(\n7段数码管显示驱动_1_seg_5 ), .d(\n7段数码管显示驱动_1_seg_6 ), .c(\n7段数码管显示驱动_1_seg_7 ), .dp(1'b1));

  // Notes on the sheet:
  //   按键编码值
  //   16进制显示
  //   7段管显示
endmodule

// 编码器
module \_5输入按键编码器设计  (
  input  In1,
  input  In2,
  input  In3,
  input  In4,
  input  In5,
  output Out1,
  output Out2,
  output Out3
);

  wire and_1_out, and_2_out, and_3_out, and_4_out, and_5_out, not_1_out, not_2_out, not_3_out, not_4_out,
       not_5_out, not_6_out, not_7_out, not_8_out, not_9_out, not_10_out;

  not not_1 (not_1_out, In4);
  not not_2 (not_2_out, In2);
  not not_3 (not_3_out, In4);
  not not_4 (not_4_out, In4);
  not not_5 (not_5_out, In5);
  not not_6 (not_6_out, In1);
  not not_7 (not_7_out, In3);
  not not_8 (not_8_out, In4);
  not not_9 (not_9_out, In4);
  not not_10 (not_10_out, In5);
  or or_1 (Out3, In5, In4);
  and and_1 (and_1_out, In3, not_1_out);
  and and_2 (and_2_out, In1, not_2_out, not_3_out);
  and and_3 (and_3_out, In3, not_4_out, not_5_out);
  and and_4 (and_4_out, not_6_out, In2, not_7_out, not_8_out);
  and and_5 (and_5_out, In2, not_9_out, not_10_out);
  or or_2 (Out1, In5, and_1_out, and_2_out);
  or or_3 (Out2, and_3_out, and_4_out, and_5_out);
endmodule

// 数码管驱动
module \_7段数码管显示驱动  (
  input  X0,
  input  X1,
  input  X2,
  input  X3,
  output Seg_1,
  output Seg_2,
  output Seg_3,
  output Seg_4,
  output Seg_5,
  output Seg_6,
  output Seg_7
);

  wire and_1_out, and_2_out, and_3_out, and_4_out, and_5_out, and_6_out, and_7_out, and_8_out, and_9_out,
       and_10_out, and_11_out, and_12_out, and_13_out, and_14_out, and_15_out, and_16_out, and_17_out,
       and_18_out, and_19_out, and_20_out, and_21_out, and_22_out, not_1_out, not_2_out, not_3_out,
       not_4_out, not_5_out, not_6_out, not_7_out, not_8_out, not_9_out, not_10_out, not_11_out, not_12_out,
       not_13_out, not_14_out, not_15_out, not_16_out, not_17_out, not_18_out, not_19_out, not_20_out,
       not_21_out, not_22_out, not_23_out, not_24_out, not_25_out, not_26_out, not_27_out, not_28_out,
       not_29_out, not_30_out, not_31_out, not_32_out, not_33_out, not_34_out, not_35_out, not_36_out,
       not_37_out, not_38_out, not_39_out, not_40_out, not_41_out, not_42_out, not_43_out;

  not not_1 (not_1_out, X0);
  not not_2 (not_2_out, X1);
  not not_3 (not_3_out, X0);
  not not_4 (not_4_out, X2);
  not not_5 (not_5_out, X0);
  not not_6 (not_6_out, X1);
  not not_7 (not_7_out, X2);
  not not_8 (not_8_out, X3);
  not not_9 (not_9_out, X0);
  and and_1 (and_1_out, not_9_out, not_10_out, not_11_out);
  not not_10 (not_10_out, X2);
  not not_11 (not_11_out, X3);
  not not_12 (not_12_out, X1);
  not not_13 (not_13_out, X2);
  and and_2 (and_2_out, not_12_out, not_13_out, not_14_out);
  not not_14 (not_14_out, X3);
  not not_15 (not_15_out, X0);
  and and_3 (and_3_out, not_15_out, X1, X3);
  not not_16 (not_16_out, X1);
  not not_17 (not_17_out, X2);
  and and_4 (and_4_out, not_16_out, not_17_out, not_18_out);
  not not_18 (not_18_out, X3);
  not not_19 (not_19_out, X0);
  and and_5 (and_5_out, not_19_out, X2);
  not not_20 (not_20_out, X0);
  and and_6 (and_6_out, not_20_out, X1, X3);
  not not_21 (not_21_out, X0);
  and and_7 (and_7_out, not_21_out, not_22_out);
  not not_22 (not_22_out, X1);
  not not_23 (not_23_out, X0);
  and and_8 (and_8_out, not_23_out, not_24_out);
  not not_24 (not_24_out, X3);
  not not_25 (not_25_out, X1);
  not not_26 (not_26_out, X2);
  and and_9 (and_9_out, not_25_out, not_26_out, not_27_out);
  not not_27 (not_27_out, X3);
  not not_28 (not_28_out, X0);
  and and_10 (and_10_out, not_28_out, X2);
  not not_29 (not_29_out, X0);
  not not_30 (not_30_out, X1);
  not not_31 (not_31_out, X3);
  not not_32 (not_32_out, X0);
  not not_33 (not_33_out, X1);
  not not_34 (not_34_out, X2);
  and and_11 (and_11_out, not_33_out, not_34_out, not_35_out);
  not not_35 (not_35_out, X3);
  not not_36 (not_36_out, X0);
  and and_12 (and_12_out, not_36_out, not_37_out, X2);
  not not_37 (not_37_out, X1);
  not not_38 (not_38_out, X0);
  and and_13 (and_13_out, not_38_out, X1, X3);
  not not_39 (not_39_out, X1);
  and and_14 (and_14_out, not_39_out, not_40_out, not_41_out);
  not not_40 (not_40_out, X2);
  not not_41 (not_41_out, X3);
  not not_42 (not_42_out, X0);
  and and_15 (and_15_out, not_42_out, X3);
  not not_43 (not_43_out, X0);
  and and_16 (and_16_out, not_43_out, X1);
  and and_17 (and_17_out, not_1_out, not_2_out, X2);
  and and_18 (and_18_out, not_3_out, X1, not_4_out);
  and and_19 (and_19_out, not_5_out, X1, X3);
  and and_20 (and_20_out, X0, not_6_out, not_7_out, not_8_out);
  or or_1 (Seg_2, and_1_out, and_2_out, and_3_out);
  or or_2 (Seg_3, and_4_out, and_5_out, and_6_out);
  or or_3 (Seg_4, and_7_out, and_8_out, and_9_out, and_10_out);
  and and_21 (and_21_out, not_29_out, not_30_out, not_31_out);
  or or_4 (Seg_5, and_21_out, and_22_out);
  and and_22 (and_22_out, not_32_out, X1, X2, X3);
  or or_5 (Seg_6, and_11_out, and_12_out, and_13_out);
  or or_6 (Seg_7, and_14_out, and_15_out, and_16_out);
  or or_7 (Seg_1, and_17_out, and_18_out, and_19_out, and_20_out);
endmodule

module \数码管驱动自动测试  (
);

  wire clock_1_out, \n7段数码管显示驱动_1_seg_1 , \n7段数码管显示驱动_1_seg_2 , \n7段数码管显示驱动_1_seg_3 , \n7段数码管显示驱动_1_seg_4 ,
       \n7段数码管显示驱动_1_seg_5 , \n7段数码管显示驱动_1_seg_6 , \n7段数码管显示驱动_1_seg_7 ;
  wire [3:0] counter_1_q;

  Counter #(.width(4), .max('hf), .ongoal("wrap"), .trigger("rising"), .behavior("new")) counter_1 (
    .Q(counter_1_q), .clk(clock_1_out));  // open: load, D, count, carry, clr, preset, down
  Clock #(.highDuration(1), .lowDuration(1)) clock_1 (.out(clock_1_out));
  \_7段数码管显示驱动  \u_7段数码管显示驱动_1  (
    .X0(counter_1_q[0]), .X1(counter_1_q[1]), .X2(counter_1_q[2]), .X3(counter_1_q[3]),
    .Seg_1(\n7段数码管显示驱动_1_seg_1 ), .Seg_2(\n7段数码管显示驱动_1_seg_2 ), .Seg_3(\n7段数码管显示驱动_1_seg_3 ),
    .Seg_4(\n7段数码管显示驱动_1_seg_4 ), .Seg_5(\n7段数码管显示驱动_1_seg_5 ), .Seg_6(\n7段数码管显示驱动_1_seg_6 ),
    .Seg_7(\n7段数码管显示驱动_1_seg_7 ));
  _7_Segment_Display #(.active("true")) u_7_segment_display_1 (
    .g(\n7段数码管显示驱动_1_seg_1 ), .f(\n7段数码管显示驱动_1_seg_2 ), .a(\n7段数码管显示驱动_1_seg_3 ), .b(\n7段数码管显示驱动_1_seg_4 ),
    .e(\n7段数码管显示驱动_1_seg_5 ), .d(\n7段数码管显示驱动_1_seg_6 ), .c(\n7段数码管显示驱动_1_seg_7 ), .dp(1'b1));

  // Notes on the sheet:
  //   计数器
endmodule

module \_2路选择器_1位  (
  input  X0,
  input  X1,
  input  Sel,
  output Out1
);

  wire and_1_out, and_2_out, not_1_out;

  not not_1 (not_1_out, Sel);
  and and_1 (and_1_out, X1, Sel);
  and and_2 (and_2_out, X0, not_1_out);
  or or_1 (Out1, and_1_out, and_2_out);
endmodule

// 1位比较器
module \_1位无符号比较器  (
  input  X,
  input  Y,
  output Bigger,
  output Equal,
  output Less
);

  wire and_2_out, and_3_out, not_1_out, not_2_out, not_3_out, not_4_out;

  not not_1 (not_1_out, Y);
  not not_2 (not_2_out, X);
  not not_3 (not_3_out, Y);
  not not_4 (not_4_out, X);
  and and_1 (Bigger, X, not_1_out);
  and and_2 (and_2_out, not_2_out, not_3_out);
  and and_3 (and_3_out, X, Y);
  and and_4 (Less, not_4_out, Y);
  or or_1 (Equal, and_2_out, and_3_out);
endmodule

// 4位比较器
module \_4位无符号比较器  (
  input  X3,
  input  Y3,
  input  X2,
  input  Y2,
  input  X1,
  input  Y1,
  input  X0,
  input  Y0,
  output Bigger,
  output Equal,
  output Less
);

  wire and_1_out, and_2_out, and_3_out, and_4_out, and_5_out, and_6_out, \n1位无符号比较器_1_bigger ,
       \n1位无符号比较器_1_equal , \n1位无符号比较器_1_less , \n1位无符号比较器_2_bigger , \n1位无符号比较器_2_equal ,
       \n1位无符号比较器_2_less , \n1位无符号比较器_3_bigger , \n1位无符号比较器_3_equal , \n1位无符号比较器_3_less ,
       \n1位无符号比较器_4_bigger , \n1位无符号比较器_4_equal , \n1位无符号比较器_4_less ;

  \_1位无符号比较器  \u_1位无符号比较器_1  (
    .X(X3), .Y(Y3), .Bigger(\n1位无符号比较器_1_bigger ), .Equal(\n1位无符号比较器_1_equal ), .Less(\n1位无符号比较器_1_less ));
  \_1位无符号比较器  \u_1位无符号比较器_2  (
    .X(X2), .Y(Y2), .Bigger(\n1位无符号比较器_2_bigger ), .Equal(\n1位无符号比较器_2_equal ), .Less(\n1位无符号比较器_2_less ));
  \_1位无符号比较器  \u_1位无符号比较器_3  (
    .X(X1), .Y(Y1), .Bigger(\n1位无符号比较器_3_bigger ), .Equal(\n1位无符号比较器_3_equal ), .Less(\n1位无符号比较器_3_less ));
  \_1位无符号比较器  \u_1位无符号比较器_4  (
    .X(X0), .Y(Y0), .Bigger(\n1位无符号比较器_4_bigger ), .Equal(\n1位无符号比较器_4_equal ), .Less(\n1位无符号比较器_4_less ));
  and and_1 (and_1_out, \n1位无符号比较器_1_equal , \n1位无符号比较器_2_bigger );
  and and_2 (and_2_out, \n1位无符号比较器_1_equal , \n1位无符号比较器_2_equal , \n1位无符号比较器_3_bigger );
  and and_3 (and_3_out, \n1位无符号比较器_1_equal , \n1位无符号比较器_3_equal , \n1位无符号比较器_4_bigger );
  and and_4 (and_4_out, \n1位无符号比较器_1_equal , \n1位无符号比较器_2_less );
  and and_5 (and_5_out, \n1位无符号比较器_1_equal , \n1位无符号比较器_2_equal , \n1位无符号比较器_3_less );
  and and_6 (and_6_out, \n1位无符号比较器_1_equal , \n1位无符号比较器_3_equal , \n1位无符号比较器_4_less );
  or or_1 (Bigger, \n1位无符号比较器_1_bigger , and_1_out, and_2_out, and_3_out);
  and and_7 (Equal, \n1位无符号比较器_1_equal , \n1位无符号比较器_2_equal , \n1位无符号比较器_3_equal , \n1位无符号比较器_4_equal );
  or or_2 (Less, \n1位无符号比较器_1_less , and_4_out, and_5_out, and_6_out);
endmodule

module \_16位无符号比较器  (
  input  [3:0] X3,
  input  [3:0] Y3,
  input  [3:0] X2,
  input  [3:0] Y2,
  input  [3:0] X1,
  input  [3:0] Y1,
  input  [3:0] X0,
  input  [3:0] Y0,
  output Bigger,
  output Equal,
  output Less
);

  wire and_1_out, and_2_out, and_3_out, and_4_out, and_5_out, and_6_out, \n4位无符号比较器_1_bigger ,
       \n4位无符号比较器_1_equal , \n4位无符号比较器_1_less , \n4位无符号比较器_2_bigger , \n4位无符号比较器_2_equal ,
       \n4位无符号比较器_2_less , \n4位无符号比较器_3_bigger , \n4位无符号比较器_3_equal , \n4位无符号比较器_3_less ,
       \n4位无符号比较器_4_bigger , \n4位无符号比较器_4_equal , \n4位无符号比较器_4_less ;

  \_4位无符号比较器  \u_4位无符号比较器_1  (
    .X3(X3[3]), .Y3(X3[2]), .X2(X3[1]), .Y2(X3[0]), .X1(Y3[3]), .Y1(Y3[2]), .X0(Y3[1]), .Y0(Y3[0]),
    .Bigger(\n4位无符号比较器_1_bigger ), .Equal(\n4位无符号比较器_1_equal ), .Less(\n4位无符号比较器_1_less ));
  \_4位无符号比较器  \u_4位无符号比较器_2  (
    .X3(X2[3]), .Y3(X2[2]), .X2(X2[1]), .Y2(X2[0]), .X1(Y2[3]), .Y1(Y2[2]), .X0(Y2[1]), .Y0(Y2[0]),
    .Bigger(\n4位无符号比较器_2_bigger ), .Equal(\n4位无符号比较器_2_equal ), .Less(\n4位无符号比较器_2_less ));
  \_4位无符号比较器  \u_4位无符号比较器_3  (
    .X3(X1[3]), .Y3(X1[2]), .X2(X1[1]), .Y2(X1[0]), .X1(Y1[3]), .Y1(Y1[2]), .X0(Y1[1]), .Y0(Y1[0]),
    .Bigger(\n4位无符号比较器_3_bigger ), .Equal(\n4位无符号比较器_3_equal ), .Less(\n4位无符号比较器_3_less ));
  \_4位无符号比较器  \u_4位无符号比较器_4  (
    .X3(X0[3]), .Y3(X0[2]), .X2(X0[1]), .Y2(X0[0]), .X1(Y0[3]), .Y1(Y0[2]), .X0(Y0[1]), .Y0(Y0[0]),
    .Bigger(\n4位无符号比较器_4_bigger ), .Equal(\n4位无符号比较器_4_equal ), .Less(\n4位无符号比较器_4_less ));
  and and_1 (and_1_out, \n4位无符号比较器_1_equal , \n4位无符号比较器_2_bigger );
  and and_2 (and_2_out, \n4位无符号比较器_1_equal , \n4位无符号比较器_2_equal , \n4位无符号比较器_3_bigger );
  and and_3 (and_3_out, \n4位无符号比较器_1_equal , \n4位无符号比较器_3_equal , \n4位无符号比较器_4_bigger );
  and and_4 (and_4_out, \n4位无符号比较器_1_equal , \n4位无符号比较器_2_less );
  and and_5 (and_5_out, \n4位无符号比较器_1_equal , \n4位无符号比较器_2_equal , \n4位无符号比较器_3_less );
  and and_6 (and_6_out, \n4位无符号比较器_1_equal , \n4位无符号比较器_3_equal , \n4位无符号比较器_4_less );
  or or_1 (Bigger, \n4位无符号比较器_1_bigger , and_1_out, and_2_out, and_3_out);
  and and_7 (Equal, \n4位无符号比较器_1_equal , \n4位无符号比较器_2_equal , \n4位无符号比较器_3_equal , \n4位无符号比较器_4_equal );
  or or_2 (Less, \n4位无符号比较器_1_less , and_4_out, and_5_out, and_6_out);
endmodule
