// Logisim project storage.circ as structural Verilog: 9 circuits, main circuit ◇Cache(直接相联)
module \Cache_直接相联  (
  input  [31:0] BlockDataIn,
  input  [15:0] Addr,
  input  BlkDataReady,
  input  CLK,
  output Miss,
  output [7:0] DataOut
);

  wire and_1_out, Hit, L0, L1, L2, L3, L4, L5, L6, L7, v0, v1, v2, v3, v4, v5, v6, v7, write0, write1,
       write2, write3, write4, write5, write6, write7;
  wire [10:0] multiplexer_1_out, tag0, tag1, tag2, tag3, tag4, tag5, tag6, tag7;
  wire [11:11] multiplexer_2_out;
  wire [15:0] c0, c1, c2, c3, c4, c5, c6, c7;
  wire [31:0] DATA_2_q, DATA_3_q, DATA_4_q, DATA_5_q, DATA_6_q, DATA_7_q, DATA_8_q, DATA_q, slot;

  Register #(.width(1), .trigger("rising"), .Select("low")) Valid (
    .D(1'b1), .en(write0), .Q(v0), .clk(CLK));  // open: clr
  Register #(.width(1), .trigger("rising"), .Select("low")) Valid_2 (
    .D(1'b1), .en(write1), .Q(v1), .clk(CLK));  // open: clr
  Register #(.width(1), .trigger("rising"), .Select("low")) Valid_3 (
    .D(1'b1), .en(write2), .Q(v2), .clk(CLK));  // open: clr
  Register #(.width(1), .trigger("rising"), .Select("low")) Valid_4 (
    .D(1'b1), .en(write3), .Q(v3), .clk(CLK));  // open: clr
  Register #(.width(1), .trigger("rising"), .Select("low")) Valid_5 (
    .D(1'b1), .en(write4), .Q(v4), .clk(CLK));  // open: clr
  Register #(.width(1), .trigger("rising"), .Select("low")) Valid_6 (
    .D(1'b1), .en(write5), .Q(v5), .clk(CLK));  // open: clr
  Register #(.width(1), .trigger("rising"), .Select("low")) Valid_7 (
    .D(1'b1), .en(write6), .Q(v6), .clk(CLK));  // open: clr
  Register #(.width(1), .trigger("rising"), .Select("low")) Valid_8 (
    .D(1'b1), .en(write7), .Q(v7), .clk(CLK));  // open: clr
  Multiplexer #(.select(3), .width(11), .disabled("Z"), .enable("false")) multiplexer_1 (
    .in0(tag0), .in1(tag1), .in2(tag2), .in3(tag3), .in4(tag4), .in5(tag5), .in6(tag6), .in7(tag7),
    .out(multiplexer_1_out), .sel(Addr[4:2]));
  Multiplexer #(.select(3), .width(1), .disabled("Z"), .enable("false")) multiplexer_2 (
    .in0(v0), .in1(v1), .in2(v2), .in3(v3), .in4(v4), .in5(v5), .in6(v6), .in7(v7),
    .out(multiplexer_2_out[11]), .sel(Addr[4:2]));
  Register #(.width(11), .trigger("rising"), .Select("low")) TAG (
    .D(Addr[15:5]), .en(write0), .Q(tag0), .clk(CLK));  // open: clr
  Register #(.width(11), .trigger("rising"), .Select("low")) TAG_2 (
    .D(Addr[15:5]), .en(write1), .Q(tag1), .clk(CLK));  // open: clr
  Register #(.width(11), .trigger("rising"), .Select("low")) TAG_3 (
    .D(Addr[15:5]), .en(write2), .Q(tag2), .clk(CLK));  // open: clr
  Register #(.width(11), .trigger("rising"), .Select("low")) TAG_4 (
    .D(Addr[15:5]), .en(write3), .Q(tag3), .clk(CLK));  // open: clr
  Register #(.width(11), .trigger("rising"), .Select("low")) TAG_5 (
    .D(Addr[15:5]), .en(write4), .Q(tag4), .clk(CLK));  // open: clr
  Register #(.width(11), .trigger("rising"), .Select("low")) TAG_6 (
    .D(Addr[15:5]), .en(write5), .Q(tag5), .clk(CLK));  // open: clr
  Register #(.width(11), .trigger("rising"), .Select("low")) TAG_7 (
    .D(Addr[15:5]), .en(write6), .Q(tag6), .clk(CLK));  // open: clr
  Register #(.width(11), .trigger("rising"), .Select("low")) TAG_8 (
    .D(Addr[15:5]), .en(write7), .Q(tag7), .clk(CLK));  // open: clr
  Comparator #(.width(12), .mode("twosComplement")) comparator_1 (
    .a({multiplexer_2_out[11], multiplexer_1_out}), .b({1'b1, Addr[15:5]}), .eq(Hit));  // open: gt, lt
  not not_1 (Miss, Hit);
  Counter #(.width(16), .max('hffff), .ongoal("wrap"), .trigger("rising"), .behavior("new")) \u_淘汰计数  (
    .D({16{1'b0}}), .Q(c0), .clk(CLK), .clr(L0));  // open: load, count, carry, preset, down
  Counter #(.width(16), .max('hffff), .ongoal("wrap"), .trigger("rising"), .behavior("new")) \u_淘汰计数_2  (
    .D({16{1'b0}}), .Q(c1), .clk(CLK), .clr(L1));  // open: load, count, carry, preset, down
  Counter #(.width(16), .max('hffff), .ongoal("wrap"), .trigger("rising"), .behavior("new")) \u_淘汰计数_3  (
    .D({16{1'b0}}), .Q(c2), .clk(CLK), .clr(L2));  // open: load, count, carry, preset, down
  Counter #(.width(16), .max('hffff), .ongoal("wrap"), .trigger("rising"), .behavior("new")) \u_淘汰计数_4  (
    .D({16{1'b0}}), .Q(c3), .clk(CLK), .clr(L3));  // open: load, count, carry, preset, down
  Counter #(.width(16), .max('hffff), .ongoal("wrap"), .trigger("rising"), .behavior("new")) \u_淘汰计数_5  (
    .D({16{1'b0}}), .Q(c4), .clk(CLK), .clr(L4));  // open: load, count, carry, preset, down
  Counter #(.width(16), .max('hffff), .ongoal("wrap"), .trigger("rising"), .behavior("new")) \u_淘汰计数_6  (
    .D({16{1'b0}}), .Q(c5), .clk(CLK), .clr(L5));  // open: load, count, carry, preset, down
  Counter #(.width(16), .max('hffff), .ongoal("wrap"), .trigger("rising"), .behavior("new")) \u_淘汰计数_7  (
    .D({16{1'b0}}), .Q(c6), .clk(CLK), .clr(L6));  // open: load, count, carry, preset, down
  Counter #(.width(16), .max('hffff), .ongoal("wrap"), .trigger("rising"), .behavior("new")) \u_淘汰计数_8  (
    .D({16{1'b0}}), .Q(c7), .clk(CLK), .clr(L7));  // open: load, count, carry, preset, down
  Demultiplexer #(.select(3), .width(1), .tristate("false"), .disabled("Z"), .enable("false")) demultiplexer_1 (
    .out0(write0), .out1(write1), .out2(write2), .out3(write3), .out4(write4), .out5(write5), .out6(write6),
    .out7(write7), .in(and_1_out), .sel(Addr[4:2]));
  and and_1 (and_1_out, BlkDataReady, Miss);
  Demultiplexer #(.select(3), .width(1), .tristate("false"), .disabled("Z"), .enable("false")) demultiplexer_2 (
    .out0(L0), .out1(L1), .out2(L2), .out3(L3), .out4(L4), .out5(L5), .out6(L6), .out7(L7), .in(Hit),
    .sel(Addr[4:2]));
  Register #(.width(32), .trigger("rising"), .Select("low")) DATA (
    .D(BlockDataIn), .en(write0), .Q(DATA_q), .clk(CLK));  // open: clr
  Register #(.width(32), .trigger("rising"), .Select("low")) DATA_2 (
    .D(BlockDataIn), .en(write1), .Q(DATA_2_q), .clk(CLK));  // open: clr
  Register #(.width(32), .trigger("rising"), .Select("low")) DATA_3 (
    .D(BlockDataIn), .en(write2), .Q(DATA_3_q), .clk(CLK));  // open: clr
  Register #(.width(32), .trigger("rising"), .Select("low")) DATA_4 (
    .D(BlockDataIn), .en(write3), .Q(DATA_4_q), .clk(CLK));  // open: clr
  Register #(.width(32), .trigger("rising"), .Select("low")) DATA_5 (
    .D(BlockDataIn), .en(write4), .Q(DATA_5_q), .clk(CLK));  // open: clr
  Register #(.width(32), .trigger("rising"), .Select("low")) DATA_6 (
    .D(BlockDataIn), .en(write5), .Q(DATA_6_q), .clk(CLK));  // open: clr
  Register #(.width(32), .trigger("rising"), .Select("low")) DATA_7 (
    .D(BlockDataIn), .en(write6), .Q(DATA_7_q), .clk(CLK));  // open: clr
  Register #(.width(32), .trigger("rising"), .Select("low")) DATA_8 (
    .D(BlockDataIn), .en(write7), .Q(DATA_8_q), .clk(CLK));  // open: clr
  assign slot = L0 ? DATA_q : 32'bz;  // Controlled_Buffer controlled_buffer_1
  assign slot = L1 ? DATA_2_q : 32'bz;  // Controlled_Buffer controlled_buffer_2
  assign slot = L2 ? DATA_3_q : 32'bz;  // Controlled_Buffer controlled_buffer_3
  assign slot = L3 ? DATA_4_q : 32'bz;  // Controlled_Buffer controlled_buffer_4
  assign slot = L4 ? DATA_5_q : 32'bz;  // Controlled_Buffer controlled_buffer_5
  assign slot = L5 ? DATA_6_q : 32'bz;  // Controlled_Buffer controlled_buffer_6
  assign slot = L6 ? DATA_7_q : 32'bz;  // Controlled_Buffer controlled_buffer_7
  assign slot = L7 ? DATA_8_q : 32'bz;  // Controlled_Buffer controlled_buffer_8
  Multiplexer #(.select(2), .width(8), .disabled("Z"), .enable("false")) multiplexer_3 (
    .in0(slot[7:0]), .in1(slot[15:8]), .in2(slot[23:16]), .in3(slot[31:24]), .out(DataOut), .sel(Addr[1:0]));

  // Other names for the same wires on the sheet: tag[10:0] = Addr[15:5]; 字节地址[15:0] = Addr; Blk[31:0] = BlockDataIn;
  //   BlkReady = BlkDataReady; offset[1:0] = Addr[1:0]; index[2:0] = Addr[4:2]

  // Notes on the sheet:
  //   输入引脚区
  //   请勿增改引脚，请勿修改子电路封装
  //   16位
  //   电路功能：利用上面给定的隧道构建8行的Cache，cache映射方式自选
  //   请在下方利用上方输入输出引脚的隧道信号构建电路，ctrl+d复制选择部件
  //   输出引脚区
endmodule

module \Cache_全相联  (
  input  [31:0] BlockDataIn,
  input  [15:0] Addr,
  input  BlkDataReady,
  input  CLK,
  output Miss,
  output [7:0] DataOut
);

  wire and_1_out, and_10_out, and_11_out, and_12_out, and_13_out, and_14_out, and_15_out, and_16_out,
       and_17_out, and_18_out, and_19_out, and_20_out, and_21_out, comparator_1_eq, comparator_2_eq,
       comparator_3_eq, comparator_4_eq, comparator_5_eq, comparator_6_eq, comparator_7_eq, comparator_8_eq,
       FULL, Hit, L0, L1, L2, L3, L4, L5, L6, L7, not_1_out, not_2_out, not_3_out, not_4_out, not_5_out,
       not_6_out, not_7_out, not_8_out, not_9_out, not_10_out, not_11_out, not_12_out, v0, v1, v2, v3, v4,
       v5, v6, v7, write0, write1, write2, write3, write4, write5, write6, write7;
  wire [2:0] \max3_归并比较_1_max_num , \max3_归并比较_2_max_num , \max3_归并比较_3_max_num , \max3_归并比较_4_max_num ,
       \max3_归并比较_5_max_num , \max3_归并比较_6_max_num , multiplexer_2_out, out, row;
  wire [13:0] tag0, tag1, tag2, tag3, tag4, tag5, tag6, tag7;
  wire [15:0] c0, c1, c2, c3, c4, c5, c6, c7, \max3_归并比较_1_max , \max3_归并比较_2_max , \max3_归并比较_3_max ,
       \max3_归并比较_4_max , \max3_归并比较_5_max , \max3_归并比较_6_max ;
  wire [31:0] DATA_2_q, DATA_3_q, DATA_4_q, DATA_5_q, DATA_6_q, DATA_7_q, DATA_8_q, DATA_q, slot;

  Register #(.width(1), .trigger("rising"), .Select("low")) Valid (
    .D(1'b1), .en(write0), .Q(v0), .clk(CLK));  // open: clr
  Register #(.width(1), .trigger("rising"), .Select("low")) Valid_2 (
    .D(1'b1), .en(write1), .Q(v1), .clk(CLK));  // open: clr
  Register #(.width(1), .trigger("rising"), .Select("low")) Valid_3 (
    .D(1'b1), .en(write2), .Q(v2), .clk(CLK));  // open: clr
  Register #(.width(1), .trigger("rising"), .Select("low")) Valid_4 (
    .D(1'b1), .en(write3), .Q(v3), .clk(CLK));  // open: clr
  Register #(.width(1), .trigger("rising"), .Select("low")) Valid_5 (
    .D(1'b1), .en(write4), .Q(v4), .clk(CLK));  // open: clr
  Register #(.width(1), .trigger("rising"), .Select("low")) Valid_6 (
    .D(1'b1), .en(write5), .Q(v5), .clk(CLK));  // open: clr
  Register #(.width(1), .trigger("rising"), .Select("low")) Valid_7 (
    .D(1'b1), .en(write6), .Q(v6), .clk(CLK));  // open: clr
  Register #(.width(1), .trigger("rising"), .Select("low")) Valid_8 (
    .D(1'b1), .en(write7), .Q(v7), .clk(CLK));  // open: clr
  \Max3_归并比较  \max3_归并比较_1  (
    .Y(c1), .X(c0), .Y_num(3'b001), .X_num(3'b000), .MAX(\max3_归并比较_1_max ), .Max_num(\max3_归并比较_1_max_num ));
  \Max3_归并比较  \max3_归并比较_2  (
    .Y(c3), .X(c2), .Y_num(3'b011), .X_num(3'b010), .MAX(\max3_归并比较_2_max ), .Max_num(\max3_归并比较_2_max_num ));
  \Max3_归并比较  \max3_归并比较_3  (
    .Y(c5), .X(c4), .Y_num(3'b101), .X_num(3'b100), .MAX(\max3_归并比较_3_max ), .Max_num(\max3_归并比较_3_max_num ));
  \Max3_归并比较  \max3_归并比较_4  (
    .Y(c7), .X(c6), .Y_num(3'b111), .X_num(3'b110), .MAX(\max3_归并比较_4_max ), .Max_num(\max3_归并比较_4_max_num ));
  \Max3_归并比较  \max3_归并比较_5  (
    .Y(\max3_归并比较_2_max ), .X(\max3_归并比较_1_max ), .Y_num(\max3_归并比较_2_max_num ),
    .X_num(\max3_归并比较_1_max_num ), .MAX(\max3_归并比较_5_max ), .Max_num(\max3_归并比较_5_max_num ));
  \Max3_归并比较  \max3_归并比较_6  (
    .Y(\max3_归并比较_4_max ), .X(\max3_归并比较_3_max ), .Y_num(\max3_归并比较_4_max_num ),
    .X_num(\max3_归并比较_3_max_num ), .MAX(\max3_归并比较_6_max ), .Max_num(\max3_归并比较_6_max_num ));
  Register #(.width(14), .trigger("rising"), .Select("low")) TAG (
    .D(Addr[15:2]), .en(write0), .Q(tag0), .clk(CLK));  // open: clr
  Register #(.width(14), .trigger("rising"), .Select("low")) TAG_2 (
    .D(Addr[15:2]), .en(write1), .Q(tag1), .clk(CLK));  // open: clr
  Register #(.width(14), .trigger("rising"), .Select("low")) TAG_3 (
    .D(Addr[15:2]), .en(write2), .Q(tag2), .clk(CLK));  // open: clr
  Register #(.width(14), .trigger("rising"), .Select("low")) TAG_4 (
    .D(Addr[15:2]), .en(write3), .Q(tag3), .clk(CLK));  // open: clr
  Register #(.width(14), .trigger("rising"), .Select("low")) TAG_5 (
    .D(Addr[15:2]), .en(write4), .Q(tag4), .clk(CLK));  // open: clr
  Register #(.width(14), .trigger("rising"), .Select("low")) TAG_6 (
    .D(Addr[15:2]), .en(write5), .Q(tag5), .clk(CLK));  // open: clr
  Register #(.width(14), .trigger("rising"), .Select("low")) TAG_7 (
    .D(Addr[15:2]), .en(write6), .Q(tag6), .clk(CLK));  // open: clr
  Register #(.width(14), .trigger("rising"), .Select("low")) TAG_8 (
    .D(Addr[15:2]), .en(write7), .Q(tag7), .clk(CLK));  // open: clr
  \Max3_归并比较  \max3_归并比较_7  (
    .Y(\max3_归并比较_6_max ), .X(\max3_归并比较_5_max ), .Y_num(\max3_归并比较_6_max_num ),
    .X_num(\max3_归并比较_5_max_num ), .Max_num(out));  // open: MAX
  Counter #(.width(16), .max('hffff), .ongoal("wrap"), .trigger("rising"), .behavior("new")) \u_淘汰计数  (
    .D({16{1'b0}}), .Q(c0), .clk(CLK), .clr(L0));  // open: load, count, carry, preset, down
  Counter #(.width(16), .max('hffff), .ongoal("wrap"), .trigger("rising"), .behavior("new")) \u_淘汰计数_2  (
    .D({16{1'b0}}), .Q(c1), .clk(CLK), .clr(L1));  // open: load, count, carry, preset, down
  Counter #(.width(16), .max('hffff), .ongoal("wrap"), .trigger("rising"), .behavior("new")) \u_淘汰计数_3  (
    .D({16{1'b0}}), .Q(c2), .clk(CLK), .clr(L2));  // open: load, count, carry, preset, down
  Counter #(.width(16), .max('hffff), .ongoal("wrap"), .trigger("rising"), .behavior("new")) \u_淘汰计数_4  (
    .D({16{1'b0}}), .Q(c3), .clk(CLK), .clr(L3));  // open: load, count, carry, preset, down
  Counter #(.width(16), .max('hffff), .ongoal("wrap"), .trigger("rising"), .behavior("new")) \u_淘汰计数_5  (
    .D({16{1'b0}}), .Q(c4), .clk(CLK), .clr(L4));  // open: load, count, carry, preset, down
  Counter #(.width(16), .max('hffff), .ongoal("wrap"), .trigger("rising"), .behavior("new")) \u_淘汰计数_6  (
    .D({16{1'b0}}), .Q(c5), .clk(CLK), .clr(L5));  // open: load, count, carry, preset, down
  Counter #(.width(16), .max('hffff), .ongoal("wrap"), .trigger("rising"), .behavior("new")) \u_淘汰计数_7  (
    .D({16{1'b0}}), .Q(c6), .clk(CLK), .clr(L6));  // open: load, count, carry, preset, down
  Counter #(.width(16), .max('hffff), .ongoal("wrap"), .trigger("rising"), .behavior("new")) \u_淘汰计数_8  (
    .D({16{1'b0}}), .Q(c7), .clk(CLK), .clr(L7));  // open: load, count, carry, preset, down
  Register #(.width(32), .trigger("rising"), .Select("low")) DATA (
    .D(BlockDataIn), .en(write0), .Q(DATA_q), .clk(CLK));  // open: clr
  Register #(.width(32), .trigger("rising"), .Select("low")) DATA_2 (
    .D(BlockDataIn), .en(write1), .Q(DATA_2_q), .clk(CLK));  // open: clr
  Register #(.width(32), .trigger("rising"), .Select("low")) DATA_3 (
    .D(BlockDataIn), .en(write2), .Q(DATA_3_q), .clk(CLK));  // open: clr
  Register #(.width(32), .trigger("rising"), .Select("low")) DATA_4 (
    .D(BlockDataIn), .en(write3), .Q(DATA_4_q), .clk(CLK));  // open: clr
  Register #(.width(32), .trigger("rising"), .Select("low")) DATA_5 (
    .D(BlockDataIn), .en(write4), .Q(DATA_5_q), .clk(CLK));  // open: clr
  Register #(.width(32), .trigger("rising"), .Select("low")) DATA_6 (
    .D(BlockDataIn), .en(write5), .Q(DATA_6_q), .clk(CLK));  // open: clr
  Register #(.width(32), .trigger("rising"), .Select("low")) DATA_7 (
    .D(BlockDataIn), .en(write6), .Q(DATA_7_q), .clk(CLK));  // open: clr
  Register #(.width(32), .trigger("rising"), .Select("low")) DATA_8 (
    .D(BlockDataIn), .en(write7), .Q(DATA_8_q), .clk(CLK));  // open: clr
  assign slot = L0 ? DATA_q : 32'bz;  // Controlled_Buffer controlled_buffer_1
  assign slot = L1 ? DATA_2_q : 32'bz;  // Controlled_Buffer controlled_buffer_2
  assign slot = L2 ? DATA_3_q : 32'bz;  // Controlled_Buffer controlled_buffer_3
  assign slot = L3 ? DATA_4_q : 32'bz;  // Controlled_Buffer controlled_buffer_4
  assign slot = L4 ? DATA_5_q : 32'bz;  // Controlled_Buffer controlled_buffer_5
  assign slot = L5 ? DATA_6_q : 32'bz;  // Controlled_Buffer controlled_buffer_6
  assign slot = L6 ? DATA_7_q : 32'bz;  // Controlled_Buffer controlled_buffer_7
  assign slot = L7 ? DATA_8_q : 32'bz;  // Controlled_Buffer controlled_buffer_8
  Multiplexer #(.select(2), .width(8), .disabled("Z"), .enable("false")) multiplexer_1 (
    .in0(slot[7:0]), .in1(slot[15:8]), .in2(slot[23:16]), .in3(slot[31:24]), .out(DataOut), .sel(Addr[1:0]));
  and and_1 (and_1_out, BlkDataReady, Miss);
  Multiplexer #(.select(1), .width(3), .disabled("Z"), .enable("false")) multiplexer_2 (
    .in0(row), .in1(out), .out(multiplexer_2_out), .sel(FULL));
  Comparator #(.width(14), .mode("unsigned")) comparator_1 (
    .a(Addr[15:2]), .b(tag0), .eq(comparator_1_eq));  // open: gt, lt
  Comparator #(.width(14), .mode("unsigned")) comparator_2 (
    .a(Addr[15:2]), .b(tag1), .eq(comparator_2_eq));  // open: gt, lt
  Comparator #(.width(14), .mode("unsigned")) comparator_3 (
    .a(Addr[15:2]), .b(tag2), .eq(comparator_3_eq));  // open: gt, lt
  Comparator #(.width(14), .mode("unsigned")) comparator_4 (
    .a(Addr[15:2]), .b(tag3), .eq(comparator_4_eq));  // open: gt, lt
  Comparator #(.width(14), .mode("unsigned")) comparator_5 (
    .a(Addr[15:2]), .b(tag4), .eq(comparator_5_eq));  // open: gt, lt
  Comparator #(.width(14), .mode("unsigned")) comparator_6 (
    .a(Addr[15:2]), .b(tag5), .eq(comparator_6_eq));  // open: gt, lt
  Comparator #(.width(14), .mode("unsigned")) comparator_7 (
    .a(Addr[15:2]), .b(tag6), .eq(comparator_7_eq));  // open: gt, lt
  Comparator #(.width(14), .mode("unsigned")) comparator_8 (
    .a(Addr[15:2]), .b(tag7), .eq(comparator_8_eq));  // open: gt, lt
  Demultiplexer #(.select(3), .width(1), .tristate("false"), .disabled("Z"), .enable("false")) demultiplexer_1 (
    .out0(write0), .out1(write1), .out2(write2), .out3(write3), .out4(write4), .out5(write5), .out6(write6),
    .out7(write7), .in(and_1_out), .sel(multiplexer_2_out));
  and and_2 (L0, comparator_1_eq, v0);
  and and_3 (L1, comparator_2_eq, v1);
  and and_4 (L2, comparator_3_eq, v2);
  and and_5 (L3, comparator_4_eq, v3);
  and and_6 (L4, comparator_5_eq, v4);
  and and_7 (L5, comparator_6_eq, v5);
  and and_8 (L6, comparator_7_eq, v6);
  and and_9 (L7, comparator_8_eq, v7);
  not not_1 (not_1_out, v4);
  not not_2 (not_2_out, v5);
  not not_3 (not_3_out, v6);
  not not_4 (not_4_out, v7);
  not not_5 (not_5_out, v2);
  not not_6 (not_6_out, v3);
  not not_7 (not_7_out, v6);
  not not_8 (not_8_out, v7);
  not not_9 (not_9_out, v1);
  not not_10 (not_10_out, v3);
  not not_11 (not_11_out, v5);
  not not_12 (not_12_out, v7);
  and and_10 (and_10_out, not_1_out, v3, v2, v1, v0);
  and and_11 (and_11_out, not_2_out, v4, v3, v2, v1, v0);
  and and_12 (and_12_out, not_3_out, v5, v4, v3, v2, v1, v0);
  and and_13 (and_13_out, not_4_out, v6, v5, v4, v3, v2, v1, v0);
  and and_14 (and_14_out, not_5_out, v1, v0);
  and and_15 (and_15_out, not_6_out, v2, v1, v0);
  and and_16 (and_16_out, not_7_out, v5, v4, v3, v2, v1, v0);
  and and_17 (and_17_out, not_8_out, v6, v5, v4, v3, v2, v1, v0);
  and and_18 (and_18_out, not_9_out, v0);
  and and_19 (and_19_out, not_10_out, v2, v1, v0);
  and and_20 (and_20_out, not_11_out, v4, v3, v2, v1, v0);
  and and_21 (and_21_out, not_12_out, v6, v5, v4, v3, v2, v1, v0);
  or or_1 (row[2], and_10_out, and_11_out, and_12_out, and_13_out);
  or or_2 (row[1], and_14_out, and_15_out, and_16_out, and_17_out);
  or or_3 (row[0], and_18_out, and_19_out, and_20_out, and_21_out);
  or or_4 (Hit, L0, L1, L2, L3, L4, L5, L6, L7);
  not not_13 (Miss, Hit);
  and and_22 (FULL, v0, v1, v2, v3, v4, v5, v6, v7);

  // Other names for the same wires on the sheet: Blk[31:0] = BlockDataIn; BlkReady = BlkDataReady;
  //   offset[1:0] = Addr[1:0]; 字节地址[15:0] = Addr; tag[13:0] = Addr[15:2]

  // Notes on the sheet:
  //   输入引脚区
  //   请勿增改引脚，请勿修改子电路封装
  //   16位
  //   电路功能：利用上面给定的隧道构建8行的Cache，cache映射方式自选
  //   请在下方利用上方输入输出引脚的隧道信号构建电路，ctrl+d复制选择部件
  //   输出引脚区
endmodule

module \Cache_2路组相联  (
  input  [31:0] BlockDataIn,
  input  [15:0] Addr,
  input  BlkDataReady,
  input  CLK,
  output Miss,
  output [7:0] DataOut
);

  wire and_1_out, and_2_out, and_3_out, and_4_out, and_5_out, and_6_out, and_7_out, and_8_out, and_9_out,
       comparator_1_eq, comparator_2_eq, d_ff_1_q, d_ff_2_q, d_ff_3_q, d_ff_4_q, d_ff_5_q, d_ff_6_q,
       d_ff_7_q, d_ff_8_q, FULL, Hit, in, L0, L1, L2, L3, L4, L5, L6, L7, not_2_out, not_3_out, not_4_out,
       not_5_out, out, v0, v1, v2, v3, v4, v5, v6, v7, write0, write1, write2, write3, write4, write5,
       write6, write7;
  wire [0:0] multiplexer_6_out;
  wire [1:0] \max2_归并比较_1_max_num , \max2_归并比较_2_max_num , \max2_归并比较_3_max_num , \max2_归并比较_4_max_num ;
  wire [1:1] multiplexer_4_out;
  wire [11:0] tag0, tag1, tag2, tag3, tag4, tag5, tag6, tag7;
  wire [12:0] multiplexer_1_out, multiplexer_2_out;
  wire [15:0] c0, c1, c2, c3, c4, c5, c6, c7;
  wire [31:0] DATA_2_q, DATA_3_q, DATA_4_q, DATA_5_q, DATA_6_q, DATA_7_q, DATA_8_q, DATA_q, slot;

  Register #(.width(1), .trigger("rising"), .Select("low")) Valid (
    .D(1'b1), .en(write0), .Q(v0), .clk(CLK));  // open: clr
  Register #(.width(1), .trigger("rising"), .Select("low")) Valid_2 (
    .D(1'b1), .en(write1), .Q(v1), .clk(CLK));  // open: clr
  Register #(.width(1), .trigger("rising"), .Select("low")) Valid_3 (
    .D(1'b1), .en(write2), .Q(v2), .clk(CLK));  // open: clr
  Register #(.width(1), .trigger("rising"), .Select("low")) Valid_4 (
    .D(1'b1), .en(write3), .Q(v3), .clk(CLK));  // open: clr
  Register #(.width(1), .trigger("rising"), .Select("low")) Valid_5 (
    .D(1'b1), .en(write4), .Q(v4), .clk(CLK));  // open: clr
  Register #(.width(1), .trigger("rising"), .Select("low")) Valid_6 (
    .D(1'b1), .en(write5), .Q(v5), .clk(CLK));  // open: clr
  Register #(.width(1), .trigger("rising"), .Select("low")) Valid_7 (
    .D(1'b1), .en(write6), .Q(v6), .clk(CLK));  // open: clr
  Register #(.width(1), .trigger("rising"), .Select("low")) Valid_8 (
    .D(1'b1), .en(write7), .Q(v7), .clk(CLK));  // open: clr
  Register #(.width(12), .trigger("rising"), .Select("low")) TAG (
    .D(Addr[15:4]), .en(write0), .Q(tag0), .clk(CLK));  // open: clr
  Register #(.width(12), .trigger("rising"), .Select("low")) TAG_2 (
    .D(Addr[15:4]), .en(write1), .Q(tag1), .clk(CLK));  // open: clr
  Register #(.width(12), .trigger("rising"), .Select("low")) TAG_3 (
    .D(Addr[15:4]), .en(write2), .Q(tag2), .clk(CLK));  // open: clr
  Register #(.width(12), .trigger("rising"), .Select("low")) TAG_4 (
    .D(Addr[15:4]), .en(write3), .Q(tag3), .clk(CLK));  // open: clr
  Register #(.width(12), .trigger("rising"), .Select("low")) TAG_5 (
    .D(Addr[15:4]), .en(write4), .Q(tag4), .clk(CLK));  // open: clr
  Register #(.width(12), .trigger("rising"), .Select("low")) TAG_6 (
    .D(Addr[15:4]), .en(write5), .Q(tag5), .clk(CLK));  // open: clr
  Register #(.width(12), .trigger("rising"), .Select("low")) TAG_7 (
    .D(Addr[15:4]), .en(write6), .Q(tag6), .clk(CLK));  // open: clr
  Register #(.width(12), .trigger("rising"), .Select("low")) TAG_8 (
    .D(Addr[15:4]), .en(write7), .Q(tag7), .clk(CLK));  // open: clr
  Counter #(.width(16), .max('hffff), .ongoal("wrap"), .trigger("rising"), .behavior("new")) \u_淘汰计数  (
    .D({16{1'b0}}), .Q(c0), .clk(CLK), .clr(d_ff_1_q));  // open: load, count, carry, preset, down
  Counter #(.width(16), .max('hffff), .ongoal("wrap"), .trigger("rising"), .behavior("new")) \u_淘汰计数_2  (
    .D({16{1'b0}}), .Q(c1), .clk(CLK), .clr(d_ff_2_q));  // open: load, count, carry, preset, down
  Counter #(.width(16), .max('hffff), .ongoal("wrap"), .trigger("rising"), .behavior("new")) \u_淘汰计数_3  (
    .D({16{1'b0}}), .Q(c2), .clk(CLK), .clr(d_ff_3_q));  // open: load, count, carry, preset, down
  Counter #(.width(16), .max('hffff), .ongoal("wrap"), .trigger("rising"), .behavior("new")) \u_淘汰计数_4  (
    .D({16{1'b0}}), .Q(c3), .clk(CLK), .clr(d_ff_4_q));  // open: load, count, carry, preset, down
  Counter #(.width(16), .max('hffff), .ongoal("wrap"), .trigger("rising"), .behavior("new")) \u_淘汰计数_5  (
    .D({16{1'b0}}), .Q(c4), .clk(CLK), .clr(d_ff_5_q));  // open: load, count, carry, preset, down
  Counter #(.width(16), .max('hffff), .ongoal("wrap"), .trigger("rising"), .behavior("new")) \u_淘汰计数_6  (
    .D({16{1'b0}}), .Q(c5), .clk(CLK), .clr(d_ff_6_q));  // open: load, count, carry, preset, down
  Counter #(.width(16), .max('hffff), .ongoal("wrap"), .trigger("rising"), .behavior("new")) \u_淘汰计数_7  (
    .D({16{1'b0}}), .Q(c6), .clk(CLK), .clr(d_ff_7_q));  // open: load, count, carry, preset, down
  Counter #(.width(16), .max('hffff), .ongoal("wrap"), .trigger("rising"), .behavior("new")) \u_淘汰计数_8  (
    .D({16{1'b0}}), .Q(c7), .clk(CLK), .clr(d_ff_8_q));  // open: load, count, carry, preset, down
  D_Flip_Flop #(.trigger("high"), .Pre_Clr_Positions("LEGACY"), .NegatePresetClear("false"), .enable("true"), .NewFFLayout("false")) d_ff_1 (
    .clk(CLK), .D(L0), .Q(d_ff_1_q));  // open: Qn, preset, en, reset
  Register #(.width(32), .trigger("rising"), .Select("low")) DATA (
    .D(BlockDataIn), .en(write0), .Q(DATA_q), .clk(CLK));  // open: clr
  D_Flip_Flop #(.trigger("high"), .Pre_Clr_Positions("LEGACY"), .NegatePresetClear("false"), .enable("true"), .NewFFLayout("false")) d_ff_2 (
    .clk(CLK), .D(L1), .Q(d_ff_2_q));  // open: Qn, preset, en, reset
  Register #(.width(32), .trigger("rising"), .Select("low")) DATA_2 (
    .D(BlockDataIn), .en(write1), .Q(DATA_2_q), .clk(CLK));  // open: clr
  D_Flip_Flop #(.trigger("high"), .Pre_Clr_Positions("LEGACY"), .NegatePresetClear("false"), .enable("true"), .NewFFLayout("false")) d_ff_3 (
    .clk(CLK), .D(L2), .Q(d_ff_3_q));  // open: Qn, preset, en, reset
  Register #(.width(32), .trigger("rising"), .Select("low")) DATA_3 (
    .D(BlockDataIn), .en(write2), .Q(DATA_3_q), .clk(CLK));  // open: clr
  D_Flip_Flop #(.trigger("high"), .Pre_Clr_Positions("LEGACY"), .NegatePresetClear("false"), .enable("true"), .NewFFLayout("false")) d_ff_4 (
    .clk(CLK), .D(L3), .Q(d_ff_4_q));  // open: Qn, preset, en, reset
  Register #(.width(32), .trigger("rising"), .Select("low")) DATA_4 (
    .D(BlockDataIn), .en(write3), .Q(DATA_4_q), .clk(CLK));  // open: clr
  D_Flip_Flop #(.trigger("high"), .Pre_Clr_Positions("LEGACY"), .NegatePresetClear("false"), .enable("true"), .NewFFLayout("false")) d_ff_5 (
    .clk(CLK), .D(L4), .Q(d_ff_5_q));  // open: Qn, preset, en, reset
  Register #(.width(32), .trigger("rising"), .Select("low")) DATA_5 (
    .D(BlockDataIn), .en(write4), .Q(DATA_5_q), .clk(CLK));  // open: clr
  D_Flip_Flop #(.trigger("high"), .Pre_Clr_Positions("LEGACY"), .NegatePresetClear("false"), .enable("true"), .NewFFLayout("false")) d_ff_6 (
    .clk(CLK), .D(L5), .Q(d_ff_6_q));  // open: Qn, preset, en, reset
  Register #(.width(32), .trigger("rising"), .Select("low")) DATA_6 (
    .D(BlockDataIn), .en(write5), .Q(DATA_6_q), .clk(CLK));  // open: clr
  D_Flip_Flop #(.trigger("high"), .Pre_Clr_Positions("LEGACY"), .NegatePresetClear("false"), .enable("true"), .NewFFLayout("false")) d_ff_7 (
    .clk(CLK), .D(L6), .Q(d_ff_7_q));  // open: Qn, preset, en, reset
  Register #(.width(32), .trigger("rising"), .Select("low")) DATA_7 (
    .D(BlockDataIn), .en(write6), .Q(DATA_7_q), .clk(CLK));  // open: clr
  D_Flip_Flop #(.trigger("high"), .Pre_Clr_Positions("LEGACY"), .NegatePresetClear("false"), .enable("true"), .NewFFLayout("false")) d_ff_8 (
    .clk(CLK), .D(L7), .Q(d_ff_8_q));  // open: Qn, preset, en, reset
  Register #(.width(32), .trigger("rising"), .Select("low")) DATA_8 (
    .D(BlockDataIn), .en(write7), .Q(DATA_8_q), .clk(CLK));  // open: clr
  assign slot = L0 ? DATA_q : 32'bz;  // Controlled_Buffer controlled_buffer_1
  assign slot = L1 ? DATA_2_q : 32'bz;  // Controlled_Buffer controlled_buffer_2
  assign slot = L2 ? DATA_3_q : 32'bz;  // Controlled_Buffer controlled_buffer_3
  assign slot = L3 ? DATA_4_q : 32'bz;  // Controlled_Buffer controlled_buffer_4
  assign slot = L4 ? DATA_5_q : 32'bz;  // Controlled_Buffer controlled_buffer_5
  assign slot = L5 ? DATA_6_q : 32'bz;  // Controlled_Buffer controlled_buffer_6
  assign slot = L6 ? DATA_7_q : 32'bz;  // Controlled_Buffer controlled_buffer_7
  assign slot = L7 ? DATA_8_q : 32'bz;  // Controlled_Buffer controlled_buffer_8
  and and_1 (and_1_out, v0, v1);
  and and_2 (and_2_out, v2, v3);
  and and_3 (and_3_out, v4, v5);
  and and_4 (and_4_out, v6, v7);
  \Max2_归并比较  \max2_归并比较_1  (
    .Y(c1), .X(c0), .Y_num(2'b01), .X_num(2'b00), .MAX_num(\max2_归并比较_1_max_num ));  // open: MAX
  \Max2_归并比较  \max2_归并比较_2  (
    .Y(c3), .X(c2), .Y_num(2'b01), .X_num(2'b00), .MAX_num(\max2_归并比较_2_max_num ));  // open: MAX
  \Max2_归并比较  \max2_归并比较_3  (
    .Y(c5), .X(c4), .Y_num(2'b01), .X_num(2'b00), .MAX_num(\max2_归并比较_3_max_num ));  // open: MAX
  \Max2_归并比较  \max2_归并比较_4  (
    .Y(c7), .X(c6), .Y_num(2'b01), .X_num(2'b00), .MAX_num(\max2_归并比较_4_max_num ));  // open: MAX
  Multiplexer #(.select(2), .width(13), .disabled("Z"), .enable("false")) multiplexer_1 (
    .in0({tag0, v0}), .in1({tag2, v2}), .in2({tag4, v4}), .in3({tag6, v6}), .out(multiplexer_1_out),
    .sel(Addr[3:2]));
  Multiplexer #(.select(2), .width(13), .disabled("Z"), .enable("false")) multiplexer_2 (
    .in0({tag1, v1}), .in1({tag3, v3}), .in2({tag5, v5}), .in3({tag7, v7}), .out(multiplexer_2_out),
    .sel(Addr[3:2]));
  Multiplexer #(.select(2), .width(1), .disabled("Z"), .enable("false")) multiplexer_3 (
    .in0(and_1_out), .in1(and_2_out), .in2(and_3_out), .in3(and_4_out), .out(FULL), .sel(Addr[3:2]));
  Multiplexer #(.select(2), .width(2), .disabled("Z"), .enable("false")) multiplexer_4 (
    .in0(\max2_归并比较_1_max_num ), .in1(\max2_归并比较_2_max_num ), .in2(\max2_归并比较_3_max_num ),
    .in3(\max2_归并比较_4_max_num ), .out({multiplexer_4_out[1], out}), .sel(Addr[3:2]));
  Comparator #(.width(13), .mode("twosComplement")) comparator_1 (
    .a(multiplexer_1_out), .b({Addr[15:4], 1'b1}), .eq(comparator_1_eq));  // open: gt, lt
  Comparator #(.width(13), .mode("twosComplement")) comparator_2 (
    .a({Addr[15:4], 1'b1}), .b(multiplexer_2_out), .eq(comparator_2_eq));  // open: gt, lt
  Multiplexer #(.select(2), .width(8), .disabled("Z"), .enable("false")) multiplexer_5 (
    .in0(slot[7:0]), .in1(slot[15:8]), .in2(slot[23:16]), .in3(slot[31:24]), .out(DataOut), .sel(Addr[1:0]));
  Demultiplexer #(.select(2), .width(1), .tristate("false"), .disabled("Z"), .enable("false")) demultiplexer_1 (
    .out0(L0), .out1(L2), .out2(L4), .out3(L6), .in(comparator_1_eq), .sel(Addr[3:2]));
  Demultiplexer #(.select(2), .width(1), .tristate("false"), .disabled("Z"), .enable("false")) demultiplexer_2 (
    .out0(L1), .out1(L3), .out2(L5), .out3(L7), .in(comparator_2_eq), .sel(Addr[3:2]));
  or or_1 (Hit, comparator_2_eq, comparator_1_eq);
  not not_1 (Miss, Hit);
  not not_2 (not_2_out, v1);
  not not_3 (not_3_out, v3);
  not not_4 (not_4_out, v5);
  not not_5 (not_5_out, v7);
  and and_5 (and_5_out, v0, not_2_out);
  and and_6 (and_6_out, v2, not_3_out);
  and and_7 (and_7_out, v4, not_4_out);
  and and_8 (and_8_out, v6, not_5_out);
  Multiplexer #(.select(1), .width(1), .disabled("Z"), .enable("false")) multiplexer_6 (
    .in0(in), .in1(out), .out(multiplexer_6_out[0]), .sel(FULL));
  Multiplexer #(.select(2), .width(1), .disabled("Z"), .enable("false")) multiplexer_7 (
    .in0(and_5_out), .in1(and_6_out), .in2(and_7_out), .in3(and_8_out), .out(in), .sel(Addr[3:2]));
  Demultiplexer #(.select(3), .width(1), .tristate("false"), .disabled("Z"), .enable("false")) demultiplexer_3 (
    .out0(write0), .out1(write1), .out2(write2), .out3(write3), .out4(write4), .out5(write5), .out6(write6),
    .out7(write7), .in(and_9_out), .sel({Addr[3:2], multiplexer_6_out[0]}));
  and and_9 (and_9_out, Miss, BlkDataReady);

  // Other names for the same wires on the sheet: tag[11:0] = Addr[15:4]; 字节地址[15:0] = Addr; index[1:0] = Addr[3:2];
  //   Blk[31:0] = BlockDataIn; BlkReady = BlkDataReady; offset[1:0] = Addr[1:0]

  // Notes on the sheet:
  //   输入引脚区
  //   请勿增改引脚，请勿修改子电路封装
  //   电路功能：利用上面给定的隧道构建8行的Cache，cache映射方式自选
  //   请在下方利用上方输入输出引脚的隧道信号构建电路，ctrl+d复制选择部件
  //   输出引脚区
  //   16位
endmodule

module \Cache_4路组相联  (
  input  [31:0] BlockDataIn,
  input  [15:0] Addr,
  input  BlkDataReady,
  input  CLK,
  output Miss,
  output [7:0] DataOut
);

  wire and_1_out, and_2_out, and_3_out, and_4_out, and_5_out, and_6_out, and_7_out, and_8_out, and_9_out,
       and_10_out, and_11_out, comparator_1_eq, comparator_2_eq, comparator_3_eq, comparator_4_eq,
       comparator_5_eq, comparator_6_eq, comparator_7_eq, comparator_8_eq, FULL, Hit, L0, L1, L2, L3, L4, L5,
       L6, L7, not_1_out, not_2_out, not_3_out, not_4_out, not_5_out, not_6_out, not_7_out, not_8_out,
       not_9_out, or_5_out, or_6_out, v0, v1, v2, v3, v4, v5, v6, v7, write0, write1, write2, write3, write4,
       write5, write6, write7;
  wire [1:0] in, \max2_归并比较_1_max_num , \max2_归并比较_2_max_num , \max2_归并比较_3_max_num , \max2_归并比较_4_max_num ,
       \max2_归并比较_5_max_num , \max2_归并比较_6_max_num , multiplexer_1_out, or_2_out, or_4_out, out;
  wire [12:0] tag0, tag1, tag2, tag3, tag4, tag5, tag6, tag7;
  wire [15:0] c0, c1, c2, c3, c4, c5, c6, c7, \max2_归并比较_1_max , \max2_归并比较_2_max , \max2_归并比较_3_max ,
       \max2_归并比较_4_max ;
  wire [31:0] DATA_2_q, DATA_3_q, DATA_4_q, DATA_5_q, DATA_6_q, DATA_7_q, DATA_8_q, DATA_q, slot;

  Register #(.width(1), .trigger("rising"), .Select("low")) Valid (
    .D(1'b1), .en(write0), .Q(v0), .clk(CLK));  // open: clr
  Register #(.width(1), .trigger("rising"), .Select("low")) Valid_2 (
    .D(1'b1), .en(write1), .Q(v1), .clk(CLK));  // open: clr
  Register #(.width(1), .trigger("rising"), .Select("low")) Valid_3 (
    .D(1'b1), .en(write2), .Q(v2), .clk(CLK));  // open: clr
  Register #(.width(1), .trigger("rising"), .Select("low")) Valid_4 (
    .D(1'b1), .en(write3), .Q(v3), .clk(CLK));  // open: clr
  Register #(.width(1), .trigger("rising"), .Select("low")) Valid_5 (
    .D(1'b1), .en(write4), .Q(v4), .clk(CLK));  // open: clr
  Register #(.width(1), .trigger("rising"), .Select("low")) Valid_6 (
    .D(1'b1), .en(write5), .Q(v5), .clk(CLK));  // open: clr
  Register #(.width(1), .trigger("rising"), .Select("low")) Valid_7 (
    .D(1'b1), .en(write6), .Q(v6), .clk(CLK));  // open: clr
  Register #(.width(1), .trigger("rising"), .Select("low")) Valid_8 (
    .D(1'b1), .en(write7), .Q(v7), .clk(CLK));  // open: clr
  Register #(.width(13), .trigger("rising"), .Select("low")) TAG (
    .D(Addr[15:3]), .en(write0), .Q(tag0), .clk(CLK));  // open: clr
  Register #(.width(13), .trigger("rising"), .Select("low")) TAG_2 (
    .D(Addr[15:3]), .en(write1), .Q(tag1), .clk(CLK));  // open: clr
  Register #(.width(13), .trigger("rising"), .Select("low")) TAG_3 (
    .D(Addr[15:3]), .en(write2), .Q(tag2), .clk(CLK));  // open: clr
  Register #(.width(13), .trigger("rising"), .Select("low")) TAG_4 (
    .D(Addr[15:3]), .en(write3), .Q(tag3), .clk(CLK));  // open: clr
  Register #(.width(13), .trigger("rising"), .Select("low")) TAG_5 (
    .D(Addr[15:3]), .en(write4), .Q(tag4), .clk(CLK));  // open: clr
  Register #(.width(13), .trigger("rising"), .Select("low")) TAG_6 (
    .D(Addr[15:3]), .en(write5), .Q(tag5), .clk(CLK));  // open: clr
  Register #(.width(13), .trigger("rising"), .Select("low")) TAG_7 (
    .D(Addr[15:3]), .en(write6), .Q(tag6), .clk(CLK));  // open: clr
  Register #(.width(13), .trigger("rising"), .Select("low")) TAG_8 (
    .D(Addr[15:3]), .en(write7), .Q(tag7), .clk(CLK));  // open: clr
  Counter #(.width(16), .max('hffff), .ongoal("wrap"), .trigger("rising"), .behavior("new")) \u_淘汰计数  (
    .D({16{1'b0}}), .Q(c0), .clk(CLK), .clr(L0));  // open: load, count, carry, preset, down
  Counter #(.width(16), .max('hffff), .ongoal("wrap"), .trigger("rising"), .behavior("new")) \u_淘汰计数_2  (
    .D({16{1'b0}}), .Q(c1), .clk(CLK), .clr(L1));  // open: load, count, carry, preset, down
  Counter #(.width(16), .max('hffff), .ongoal("wrap"), .trigger("rising"), .behavior("new")) \u_淘汰计数_3  (
    .D({16{1'b0}}), .Q(c2), .clk(CLK), .clr(L2));  // open: load, count, carry, preset, down
  Counter #(.width(16), .max('hffff), .ongoal("wrap"), .trigger("rising"), .behavior("new")) \u_淘汰计数_4  (
    .D({16{1'b0}}), .Q(c3), .clk(CLK), .clr(L3));  // open: load, count, carry, preset, down
  Counter #(.width(16), .max('hffff), .ongoal("wrap"), .trigger("rising"), .behavior("new")) \u_淘汰计数_5  (
    .D({16{1'b0}}), .Q(c4), .clk(CLK), .clr(L4));  // open: load, count, carry, preset, down
  Counter #(.width(16), .max('hffff), .ongoal("wrap"), .trigger("rising"), .behavior("new")) \u_淘汰计数_6  (
    .D({16{1'b0}}), .Q(c5), .clk(CLK), .clr(L5));  // open: load, count, carry, preset, down
  Counter #(.width(16), .max('hffff), .ongoal("wrap"), .trigger("rising"), .behavior("new")) \u_淘汰计数_7  (
    .D({16{1'b0}}), .Q(c6), .clk(CLK), .clr(L6));  // open: load, count, carry, preset, down
  Counter #(.width(16), .max('hffff), .ongoal("wrap"), .trigger("rising"), .behavior("new")) \u_淘汰计数_8  (
    .D({16{1'b0}}), .Q(c7), .clk(CLK), .clr(L7));  // open: load, count, carry, preset, down
  Register #(.width(32), .trigger("rising"), .Select("low")) DATA (
    .D(BlockDataIn), .en(write0), .Q(DATA_q), .clk(CLK));  // open: clr
  Register #(.width(32), .trigger("rising"), .Select("low")) DATA_2 (
    .D(BlockDataIn), .en(write1), .Q(DATA_2_q), .clk(CLK));  // open: clr
  Register #(.width(32), .trigger("rising"), .Select("low")) DATA_3 (
    .D(BlockDataIn), .en(write2), .Q(DATA_3_q), .clk(CLK));  // open: clr
  Register #(.width(32), .trigger("rising"), .Select("low")) DATA_4 (
    .D(BlockDataIn), .en(write3), .Q(DATA_4_q), .clk(CLK));  // open: clr
  Register #(.width(32), .trigger("rising"), .Select("low")) DATA_5 (
    .D(BlockDataIn), .en(write4), .Q(DATA_5_q), .clk(CLK));  // open: clr
  Register #(.width(32), .trigger("rising"), .Select("low")) DATA_6 (
    .D(BlockDataIn), .en(write5), .Q(DATA_6_q), .clk(CLK));  // open: clr
  Register #(.width(32), .trigger("rising"), .Select("low")) DATA_7 (
    .D(BlockDataIn), .en(write6), .Q(DATA_7_q), .clk(CLK));  // open: clr
  Register #(.width(32), .trigger("rising"), .Select("low")) DATA_8 (
    .D(BlockDataIn), .en(write7), .Q(DATA_8_q), .clk(CLK));  // open: clr
  assign slot = L0 ? DATA_q : 32'bz;  // Controlled_Buffer controlled_buffer_1
  assign slot = L1 ? DATA_2_q : 32'bz;  // Controlled_Buffer controlled_buffer_2
  assign slot = L2 ? DATA_3_q : 32'bz;  // Controlled_Buffer controlled_buffer_3
  assign slot = L3 ? DATA_4_q : 32'bz;  // Controlled_Buffer controlled_buffer_4
  assign slot = L4 ? DATA_5_q : 32'bz;  // Controlled_Buffer controlled_buffer_5
  assign slot = L5 ? DATA_6_q : 32'bz;  // Controlled_Buffer controlled_buffer_6
  assign slot = L6 ? DATA_7_q : 32'bz;  // Controlled_Buffer controlled_buffer_7
  assign slot = L7 ? DATA_8_q : 32'bz;  // Controlled_Buffer controlled_buffer_8
  and and_1 (and_1_out, BlkDataReady, Miss);
  Multiplexer #(.select(1), .width(2), .disabled("Z"), .enable("false")) multiplexer_1 (
    .in0(in), .in1(out), .out(multiplexer_1_out), .sel(FULL));
  and and_2 (and_2_out, v0, v1, v2, v3);
  and and_3 (and_3_out, v4, v5, v6, v7);
  Demultiplexer #(.select(3), .width(1), .tristate("false"), .disabled("Z"), .enable("false")) demultiplexer_1 (
    .out0(write0), .out1(write1), .out2(write2), .out3(write3), .out4(write4), .out5(write5), .out6(write6),
    .out7(write7), .in(and_1_out), .sel({Addr[2], multiplexer_1_out}));
  Multiplexer #(.select(1), .width(1), .disabled("Z"), .enable("false")) multiplexer_2 (
    .in0(and_2_out), .in1(and_3_out), .out(FULL), .sel(Addr[2]));
  not not_1 (not_1_out, v3);
  not not_2 (not_2_out, v3);
  not not_3 (not_3_out, v7);
  not not_4 (not_4_out, v7);
  not not_5 (not_5_out, v2);
  and and_4 (and_4_out, not_5_out, v1, v0);
  and and_5 (and_5_out, not_1_out, v2, v1, v0);
  not not_6 (not_6_out, v1);
  and and_6 (and_6_out, not_6_out, v0);
  and and_7 (and_7_out, not_2_out, v2, v1, v0);
  not not_7 (not_7_out, v6);
  and and_8 (and_8_out, not_7_out, v5, v4);
  and and_9 (and_9_out, not_3_out, v6, v5, v4);
  not not_8 (not_8_out, v5);
  and and_10 (and_10_out, not_8_out, v4);
  and and_11 (and_11_out, not_4_out, v6, v5, v4);
  Multiplexer #(.select(2), .width(8), .disabled("Z"), .enable("false")) multiplexer_3 (
    .in0(slot[7:0]), .in1(slot[15:8]), .in2(slot[23:16]), .in3(slot[31:24]), .out(DataOut), .sel(Addr[1:0]));
  or or_1 (or_2_out[1], and_4_out, and_5_out);
  or or_2 (or_2_out[0], and_6_out, and_7_out);
  or or_3 (or_4_out[1], and_8_out, and_9_out);
  or or_4 (or_4_out[0], and_10_out, and_11_out);
  not not_9 (not_9_out, Addr[2]);
  Comparator #(.width(13), .mode("unsigned")) comparator_1 (
    .a(Addr[15:3]), .b(tag0), .eq(comparator_1_eq));  // open: gt, lt
  Comparator #(.width(13), .mode("unsigned")) comparator_2 (
    .a(Addr[15:3]), .b(tag1), .eq(comparator_2_eq));  // open: gt, lt
  Comparator #(.width(13), .mode("unsigned")) comparator_3 (
    .a(Addr[15:3]), .b(tag2), .eq(comparator_3_eq));  // open: gt, lt
  Comparator #(.width(13), .mode("unsigned")) comparator_4 (
    .a(Addr[15:3]), .b(tag3), .eq(comparator_4_eq));  // open: gt, lt
  Comparator #(.width(13), .mode("unsigned")) comparator_5 (
    .a(Addr[15:3]), .b(tag4), .eq(comparator_5_eq));  // open: gt, lt
  Comparator #(.width(13), .mode("unsigned")) comparator_6 (
    .a(Addr[15:3]), .b(tag5), .eq(comparator_6_eq));  // open: gt, lt
  Comparator #(.width(13), .mode("unsigned")) comparator_7 (
    .a(Addr[15:3]), .b(tag6), .eq(comparator_7_eq));  // open: gt, lt
  Comparator #(.width(13), .mode("unsigned")) comparator_8 (
    .a(Addr[15:3]), .b(tag7), .eq(comparator_8_eq));  // open: gt, lt
  and and_12 (L0, comparator_1_eq, not_9_out, v0);
  and and_13 (L1, comparator_2_eq, not_9_out, v1);
  and and_14 (L2, comparator_3_eq, not_9_out, v2);
  and and_15 (L3, comparator_4_eq, not_9_out, v3);
  and and_16 (L4, comparator_5_eq, Addr[2], v4);
  and and_17 (L5, comparator_6_eq, Addr[2], v5);
  and and_18 (L6, comparator_7_eq, Addr[2], v6);
  and and_19 (L7, comparator_8_eq, Addr[2], v7);
  Multiplexer #(.select(1), .width(2), .disabled("Z"), .enable("false")) multiplexer_4 (
    .in0(or_2_out), .in1(or_4_out), .out(in), .sel(Addr[2]));
  or or_5 (or_5_out, L0, L1, L2, L3);
  or or_6 (or_6_out, L4, L5, L6, L7);
  Multiplexer #(.select(1), .width(1), .disabled("Z"), .enable("false")) multiplexer_5 (
    .in0(or_5_out), .in1(or_6_out), .out(Hit), .sel(Addr[2]));
  \Max2_归并比较  \max2_归并比较_1  (
    .Y(c1), .X(c0), .Y_num(2'b01), .X_num(2'b00), .MAX(\max2_归并比较_1_max ), .MAX_num(\max2_归并比较_1_max_num ));
  \Max2_归并比较  \max2_归并比较_2  (
    .Y(c3), .X(c2), .Y_num(2'b11), .X_num(2'b10), .MAX(\max2_归并比较_2_max ), .MAX_num(\max2_归并比较_2_max_num ));
  \Max2_归并比较  \max2_归并比较_3  (
    .Y(c5), .X(c4), .Y_num(2'b01), .X_num(2'b00), .MAX(\max2_归并比较_3_max ), .MAX_num(\max2_归并比较_3_max_num ));
  \Max2_归并比较  \max2_归并比较_4  (
    .Y(c7), .X(c6), .Y_num(2'b11), .X_num(2'b10), .MAX(\max2_归并比较_4_max ), .MAX_num(\max2_归并比较_4_max_num ));
  not not_10 (Miss, Hit);
  \Max2_归并比较  \max2_归并比较_5  (
    .Y(\max2_归并比较_2_max ), .X(\max2_归并比较_1_max ), .Y_num(\max2_归并比较_2_max_num ),
    .X_num(\max2_归并比较_1_max_num ), .MAX_num(\max2_归并比较_5_max_num ));  // open: MAX
  \Max2_归并比较  \max2_归并比较_6  (
    .Y(\max2_归并比较_4_max ), .X(\max2_归并比较_3_max ), .Y_num(\max2_归并比较_4_max_num ),
    .X_num(\max2_归并比较_3_max_num ), .MAX_num(\max2_归并比较_6_max_num ));  // open: MAX
  Multiplexer #(.select(1), .width(2), .disabled("Z"), .enable("false")) multiplexer_6 (
    .in0(\max2_归并比较_5_max_num ), .in1(\max2_归并比较_6_max_num ), .out(out), .sel(Addr[2]));

  // Other names for the same wires on the sheet: index = Addr[2]; 字节地址[15:0] = Addr; Blk[31:0] = BlockDataIn;
  //   BlkReady = BlkDataReady; offset[1:0] = Addr[1:0]; tag[12:0] = Addr[15:3]

  // Notes on the sheet:
  //   输入引脚区
  //   请勿增改引脚，请勿修改子电路封装
  //   电路功能：利用上面给定的隧道构建8行的Cache，cache映射方式自选
  //   请在下方利用上方输入输出引脚的隧道信号构建电路，ctrl+d复制选择部件
  //   输出引脚区
  //   16位
endmodule

module \Cache自动测试  (
  input  in_1
);

  wire and_2_out, Clk, comparator_1_lt, comparator_2_eq, comparator_3_eq, controlled_buffer_1_out, EN, Error,
       Go, Hit, Miss, or_1_out, RDY, Runing;
  wire [3:0] _1, _2, _3;
  wire [7:0] Dataout, rom_2_data;
  wire [9:0] \计数器_q ;
  wire [15:0] adder_1_out, Addr, bit_extender_3_out, \cache块交换_1_byteaddrout , counter_1_q, subtractor_1_out,
       \实际命中 , \时钟周期数 , \校验和 , \缺失次数 , \访问次数 ;
  wire [31:0] bit_extender_1_out, bit_extender_2_out, \cache块交换_1_blockdatain , divider_1_out, divider_2_out,
       multiplier_1_out;
  wire [31:4] divider_2_rem, divider_3_out, divider_3_rem;

  Clock #(.highDuration(1), .lowDuration(1)) clock_1 (.out(Clk));
  // Probe on \实际命中 
  // Probe on \时钟周期数 
  not not_1 (Hit, Miss);
  Counter #(.width(10), .max('h3ff), .ongoal("wrap"), .trigger("rising"), .behavior("old")) \u_计数器  (
    .count(EN), .Q(\计数器_q ), .clk(Clk));  // open: load, D, carry, clr, preset
  and and_1 (EN, Hit, Go);
  \Cache_直接相联  \cache_直接相联_1  ();  // open: Addr, CLK, Miss, BlkDataReady, DataOut, BlockDataIn
  and and_2 (and_2_out, Miss, RDY, Runing);
  // Probe on \计数器_q 
  Counter #(.width(16), .max('hffff), .ongoal("wrap"), .trigger("rising"), .behavior("old")) counter_1 (
    .count(and_2_out), .Q(counter_1_q), .clk(Clk));  // open: load, D, carry, clr, preset
  Subtractor #(.width(16)) subtractor_1 (.a(\访问次数 ), .b(\缺失次数 ), .out(subtractor_1_out));  // open: bin, bout
  Comparator #(.width(16), .mode("twosComplement")) comparator_1 (
    .a(\访问次数 ), .b(\缺失次数 ), .lt(comparator_1_lt));  // open: gt, eq
  not not_2 (Runing, comparator_2_eq);
  Comparator #(.width(10), .mode("twosComplement")) comparator_2 (
    .a(\计数器_q ), .b(10'h100), .eq(comparator_2_eq));  // open: gt, lt
  Register #(.width(16), .trigger("rising"), .Select("low")) register_1 (
    .D(counter_1_q), .en(EN), .Q(\缺失次数 ), .clk(Clk));  // open: clr
  Multiplexer #(.select(1), .width(16), .disabled(0), .enable("false")) multiplexer_1 (
    .in0(subtractor_1_out), .in1({16{1'b0}}), .out(\实际命中 ), .sel(comparator_1_lt));
  // Probe on \缺失次数 
  // Probe on \校验和 
  ROM #(.addrWidth(10), .dataWidth(16), .Select("high")) rom_1 (.addr(\计数器_q ), .data(Addr));
  \Cache_2路组相联  \cache_2路组相联_1  ();  // open: BlockDataIn, Addr, BlkDataReady, CLK, Miss, DataOut
  Counter #(.width(16), .max('hffff), .ongoal("wrap"), .trigger("rising"), .behavior("old")) counter_2 (
    .count(EN), .Q(\访问次数 ), .clk(Clk));  // open: load, D, carry, clr, preset
  // Probe on Dataout
  assign bit_extender_1_out = {{16{1'b0}}, \实际命中 };  // Bit_Extender bit_extender_1
  // Probe on \访问次数 
  \Cache_4路组相联  \cache_4路组相联_1  (
    .BlockDataIn(\cache块交换_1_blockdatain ), .Addr(Addr), .BlkDataReady(RDY), .CLK(Clk), .Miss(Miss),
    .DataOut(Dataout));
  Multiplier #(.width(32)) multiplier_1 (
    .a(bit_extender_1_out), .b(32'h64), .out(multiplier_1_out));  // open: cin, cout
  assign bit_extender_2_out = {{16{1'b0}}, \访问次数 };  // Bit_Extender bit_extender_2
  \Cache_全相联  \cache_全相联_1  ();  // open: BlockDataIn, Addr, BlkDataReady, CLK, Miss, DataOut
  assign bit_extender_3_out = {{8{1'b0}}, Dataout};  // Bit_Extender bit_extender_3
  Divider #(.width(32)) divider_1 (
    .a(multiplier_1_out), .b(bit_extender_2_out), .out(divider_1_out));  // open: upper, rem
  LED #(.active("true")) \u_读数据出错  (.in(Error));
  LED #(.active("true")) \u_缺失  (.in(Miss));
  Pull_Resistor #(.pull(1)) pull_resistor_1 (.node(Miss));
  Adder #(.width(16)) adder_1 (.a(\校验和 ), .b(bit_extender_3_out), .out(adder_1_out));  // open: cin, cout
  Hex_Digit_Display hex_digit_display_1 (.value(_3), .dp(1'b1));
  \Cache块交换  \cache块交换_1  (
    .Addr(Addr), .CLK(Clk), .ByteAddrOut(\cache块交换_1_byteaddrout ), .ByteDataIn(rom_2_data), .Miss(Miss),
    .BlkDataReady(RDY), .BlockDataIn(\cache块交换_1_blockdatain ), .Enable(Runing));
  Register #(.width(16), .trigger("rising"), .Select("low")) \u_校验和  (
    .D(adder_1_out), .en(EN), .Q(\校验和 ), .clk(Clk));  // open: clr
  Divider #(.width(32)) divider_2 (
    .a(divider_1_out), .b(32'ha), .out(divider_2_out), .rem({divider_2_rem, _1}));  // open: upper
  Hex_Digit_Display hex_digit_display_2 (.value(_2));  // open: dp
  Hex_Digit_Display hex_digit_display_3 (.value(_1));  // open: dp
  \Cache_4路组相联  \cache_4路组相联_2  ();  // open: BlockDataIn, Addr, BlkDataReady, CLK, Miss, DataOut
  Divider #(.width(32)) divider_3 (
    .a(divider_2_out), .b(32'ha), .out({divider_3_out, _3}), .rem({divider_3_rem, _2}));  // open: upper
  ROM #(.addrWidth(16), .dataWidth(8), .Select("high")) rom_2 (.addr(\cache块交换_1_byteaddrout ), .data(rom_2_data));
  Comparator #(.width(8), .mode("twosComplement")) comparator_3 (
    .a(Addr[7:0]), .b(Dataout), .eq(comparator_3_eq));  // open: gt, lt
  assign controlled_buffer_1_out = Hit ? comparator_3_eq : 1'bz;  // Controlled_Buffer controlled_buffer_1
  Pull_Resistor #(.pull(1)) pull_resistor_2 (.node(controlled_buffer_1_out));
  or or_1 (or_1_out, controlled_buffer_1_out, ~in_1);  // OR_Gate
  not not_3 (Error, or_1_out);
  Counter #(.width(16), .max('hffff), .ongoal("wrap"), .trigger("rising"), .behavior("old")) counter_3 (
    .count(Runing), .Q(\时钟周期数 ), .clk(Clk));  // open: load, D, carry, clr, preset
  and and_3 (Go, Runing, or_1_out);

  // Other names for the same wires on the sheet: 读错误暂停 = in_1

  // Notes on the sheet:
  //   Trace存储器
  //   电路功能：测试Cache模块， ctrl+k启动时钟后，会自动对cache模块进行读数据测试，并将数据逐一读出进行校验和计算
  //   contents of rom_1 (hex, n*v repeats v):
  //   0 1 2 3 8 9 a b 10 11 12 13 20 21 22 23 8 9 a b 4 5 6 7 24 25 26 27 4 5 6 7 0 1 2 3 8 9 a b 8 9 a b
  //   20 21 22 23 28 29 2a 2b 24 25 26 27 4 5 6 7 24 25 26 27 0 1 2 3 8 9 a b 20 21 22 23 20 21 22 23 30
  //   31 32 33 4 5 6 7 24 25 26 27 4 5 6 7 0 1 2 3 8 9 a b 20 21 22 23 20 21 22 23 28 29 2a 2b 4 5 6 7 24
  //   25 26 27 24 25 26 27 0 1 2 3 8 9 a b 8 9 a b 20 21 22 23 30 31 32 33 4 5 6 7 24 25 26 27 24 25 26 27
  //   0 1 2 3 0 1 2 3 8 9 a b 20 21 22 23 28 29 2a 2b 4 5 6 7 24 25 26 27 4 5 6 7 0 1 2 3 8 9 a b 0 1 2 3
  //   20 21 22 23 30 31 32 33 24 25 26 27 4 5 6 7 24 25 26 27 0 1 2 3 8 9 a b 20 21 22 23 20 21 22 23 28
  //   29 2a 2b 4 5 6 7 24 25 26 27 4 5 6 7
  //   如果设计了不同的映射方式，可以将该电路中cache模块替换为对应Cache模块即可!
  //   ctrl+r复位，  错误暂停模式位为1时，数据命中但读出数据不正确时会暂停系统
  //   默认trace是顺序访问，所以测试系统中判断读错误的逻辑是地址和数据相等，如果更换了trace，这个逻辑不正确
  //   参数统计区
  //   命中率
  //   电路状态稳定后显示最终命中率
  //   二级存储器
  //   Cache模拟器
  //   contents of rom_2 (hex, n*v repeats v):
  //   0 1 2 3 4 5 6 7 8 9 a b c d e f 10 11 12 13 14 15 16 17 18 19 1a 1b 1c 1d 1e 1f 20 21 22 23 24 25 26
  //   27 28 29 2a 2b 2c 2d 2e 2f 30 31 32 33 34 35 36 37 38 39 3a 3b 3c 3d 3e 3f 40 41 42 43 44 45 46 47
  //   48 49 4a 4b 4c 4d 4e 4f 50 51 52 53 54 55 56 57 58 59 5a 5b 5c 5d 5e 5f 60 61 62 63 64 65 66 67 68
  //   69 6a 6b 6c 6d 6e 6f 70 71 72 73 74 75 76 77 78 79 7a 7b 7c 7d 7e 7f 80 81 82 83 84 85 86 87 88 89
  //   8a 8b 8c 8d 8e 8f 90 91 92 93 94 95 96 97 98 99 9a 9b 9c 9d 9e 9f a0 a1 a2 a3 a4 a5 a6 a7 a8 a9 aa
  //   ab ac ad ae af b0 b1 b2 b3 b4 b5 b6 b7 b8 b9 ba bb bc bd be bf c0 c1 c2 c3 c4 c5 c6 c7 c8 c9 ca cb
  //   cc cd ce cf d0 d1 d2 d3 d4 d5 d6 d7 d8 d9 da db dc dd de df e0 e1 e2 e3 e4 e5 e6 e7 e8 e9 ea eb ec
  //   ed ee ef f0 f1 f2 f3 f4 f5 f6 f7 f8 f9 fa fb fc fd fe ff 0 1 2 3 4 5 6 7 8 9 a b c d e f 10 11 12 13
  //   14 15 16 17 18 19 1a 1b 1c 1d 1e 1f 20 21 22 23 24 25 26 27 28 29 2a 2b 2c 2d 2e 2f 30 31 32 33 34
  //   35 36 37 38 39 3a 3b 3c 3d 3e 3f 40 41 42 43 44 45 46 47 48 49 4a 4b 4c 4d 4e 4f 50 51 52 53 54 55
  //   56 57 58 59 5a 5b 5c 5d 5e 5f 60 61 62 63 64 65 66 67 68 69 6a 6b 6c 6d 6e 6f 70 71 72 73 74 75 76
  //   77 78 79 7a 7b 7c 7d 7e 7f 80 81 82 83 84 85 86 87 88 89 8a 8b 8c 8d 8e 8f 90 91 92 93 94 95 96 97
  //   98 99 9a 9b 9c 9d 9e 9f a0 a1 a2 a3 a4 a5 a6 a7 a8 a9 aa ab ac ad ae af b0 b1 b2 b3 b4 b5 b6 b7 b8
  //   b9 ba bb bc bd be bf c0 c1 c2 c3 c4 c5 c6 c7 c8 c9 ca cb cc cd ce cf d0 d1 d2 d3 d4 d5 d6 d7 d8 d9
  //   da db dc dd de df e0 e1 e2 e3 e4 e5 e6 e7 e8 e9 ea eb ec ed ee ef f0 f1 f2 f3 f4 f5 f6 f7 f8 f9 fa
  //   fb fc fd fe ff 0 1 2 3 4 5 6 7 8 9 a b c d e f 10 11 12 13 14 15 16 17 18 19 1a 1b 1c 1d 1e 1f 20 21
  //   22 23 24 25 26 27 28 29 2a 2b 2c 2d 2e 2f 30 31 32 33 34 35 36 37 38 39 3a 3b 3c 3d 3e 3f 40 41 42
  //   43 44 45 46 47 48 49 4a 4b 4c 4d 4e 4f 50 51 52 53 54 55 56 57 58 59 5a 5b 5c 5d 5e 5f 60 61 62 63
  //   64 65 66 67 68 69 6a 6b 6c 6d 6e 6f 70 71 72 73 74 75 76 77 78 79 7a 7b 7c 7d 7e 7f 80 81 82 83 84
  //   85 86 87 88 89 8a 8b 8c 8d 8e 8f 90 91 92 93 94 95 96 97 98 99 9a 9b 9c 9d 9e 9f a0 a1 a2 a3 a4 a5
  //   a6 a7 a8 a9 aa ab ac ad ae af b0 b1 b2 b3 b4 b5 b6 b7 b8 b9 ba bb bc bd be bf c0 c1 c2 c3 c4 c5 c6
  //   c7 c8 c9 ca cb cc cd ce cf d0 d1 d2 d3 d4 d5 d6 d7 d8 d9 da db dc dd de df e0 e1 e2 e3 e4 e5 e6 e7
  //   e8 e9 ea eb ec ed ee ef f0 f1 f2 f3 f4 f5 f6 f7 f8 f9 fa fb fc fd fe ff 0 1 2 3 4 5 6 7 8 9 a b c d
  //   e f 10 11 12 13 14 15 16 17 18 19 1a 1b 1c 1d 1e 1f 20 21 22 23 24 25 26 27 28 29 2a 2b 2c 2d 2e 2f
  //   30 31 32 33 34 35 36 37 38 39 3a 3b 3c 3d 3e 3f 40 41 42 43 44 45 46 47 48 49 4a 4b 4c 4d 4e 4f 50
  //   51 52 53 54 55 56 57 58 59 5a 5b 5c 5d 5e 5f 60 61 62 63 64 65 66 67 68 69 6a 6b 6c 6d 6e 6f 70 71
  //   72 73 74 75 76 77 78 79 7a 7b 7c 7d 7e 7f 80 81 82 83 84 85 86 87 88 89 8a 8b 8c 8d 8e 8f 90 91 92
  //   93 94 95 96 97 98 99 9a 9b 9c 9d 9e 9f a0 a1 a2 a3 a4 a5 a6 a7 a8 a9 aa ab ac ad ae af b0 b1 b2 b3
  //   b4 b5 b6 b7 b8 b9 ba bb bc bd be bf c0 c1 c2 c3 c4 c5 c6 c7 c8 c9 ca cb cc cd ce cf d0 d1 d2 d3 d4
  //   d5 d6 d7 d8 d9 da db dc dd de df e0 e1 e2 e3 e4 e5 e6 e7 e8 e9 ea eb ec ed ee ef f0 f1 f2 f3 f4 f5
  //   f6 f7 f8 f9 fa fb fc fd fe ff 0 1 2 3 4 5 6 7 8 9 a b c d e f 10 11 12 13 14 15 16 17 18 19 1a 1b 1c
  //   1d 1e 1f 20 21 22 23 24 25 26 27 28 29 2a 2b 2c 2d 2e 2f 30 31 32 33 34 35 36 37 38 39 3a 3b 3c 3d
  //   3e 3f 40 41 42 43 44 45 46 47 48 49 4a 4b 4c 4d 4e 4f 50 51 52 53 54 55 56 57 58 59 5a 5b 5c 5d 5e
  //   5f 60 61 62 63 64 65 66 67 68 69 6a 6b 6c 6d 6e 6f 70 71 72 73 74 75 76 77 78 79 7a 7b 7c 7d 7e 7f
  //   80 81 82 83 84 85 86 87 88 89 8a 8b 8c 8d 8e 8f 90 91 92 93 94 95 96 97 98 99 9a 9b 9c 9d 9e 9f a0
  //   a1 a2 a3 a4 a5 a6 a7 a8 a9 aa ab ac ad ae af b0 b1 b2 b3 b4 b5 b6 b7 b8 b9 ba bb bc bd be bf c0 c1
  //   c2 c3 c4 c5 c6 c7 c8 c9 ca cb cc cd ce cf d0 d1 d2 d3 d4 d5 d6 d7 d8 d9 da db dc dd de df e0 e1 e2
  //   e3 e4 e5 e6 e7 e8 e9 ea eb ec ed ee ef f0 f1 f2 f3 f4 f5 f6 f7 f8 f9 fa fb fc fd fe ff
endmodule

// Max2
module \Max2_归并比较  (
  input  [15:0] Y,
  input  [15:0] X,
  input  [1:0] Y_num,
  input  [1:0] X_num,
  output [15:0] MAX,
  output [1:0] MAX_num
);

  wire comparator_1_eq, comparator_1_gt, or_1_out;

  Multiplexer #(.select(1), .width(16), .disabled("Z"), .enable("true")) multiplexer_1 (
    .in0(Y), .in1(X), .out(MAX), .sel(or_1_out), .en(1'b1));
  Comparator #(.width(16), .mode("unsigned")) comparator_1 (
    .a(X), .b(Y), .gt(comparator_1_gt), .eq(comparator_1_eq));  // open: lt
  or or_1 (or_1_out, comparator_1_gt, comparator_1_eq);
  Multiplexer #(.select(1), .width(2), .disabled("Z"), .enable("false")) multiplexer_2 (
    .in0(Y_num), .in1(X_num), .out(MAX_num), .sel(or_1_out));

  // Notes on the sheet:
  //   输出两个输入中的较大值，并输出较大值的2位编号
endmodule

// Max3
module \Max3_归并比较  (
  input  [15:0] Y,
  input  [15:0] X,
  input  [2:0] Y_num,
  input  [2:0] X_num,
  output [15:0] MAX,
  output [2:0] Max_num
);

  wire comparator_1_eq, comparator_1_gt, or_1_out;

  Multiplexer #(.select(1), .width(16), .disabled("Z"), .enable("false")) multiplexer_1 (
    .in0(Y), .in1(X), .out(MAX), .sel(or_1_out));
  Comparator #(.width(16), .mode("unsigned")) comparator_1 (
    .a(X), .b(Y), .gt(comparator_1_gt), .eq(comparator_1_eq));  // open: lt
  or or_1 (or_1_out, comparator_1_gt, comparator_1_eq);
  Multiplexer #(.select(1), .width(3), .disabled("Z"), .enable("false")) multiplexer_2 (
    .in0(Y_num), .in1(X_num), .out(Max_num), .sel(or_1_out));

  // Notes on the sheet:
  //   输出两个输入中的较大值，并输出较大值的3位编号
endmodule

module \Cache块交换  (
  input  [15:0] Addr,
  input  [7:0] ByteDataIn,
  input  Miss,
  input  Enable,
  input  CLK,
  output [15:0] ByteAddrOut,
  output [31:0] BlockDataIn,
  output BlkDataReady
);

  wire \块交换状态机_1_byte0_ready , \块交换状态机_1_byte1_ready , \块交换状态机_1_byte2_ready , \块交换状态机_1_byte3_ready ;
  wire [7:0] register_1_q, register_2_q, register_3_q, register_4_q;

  assign ByteAddrOut = \块交换状态机_1_byte0_ready  ? {Addr[15:2], 2'b00} : 16'bz;  // Controlled_Buffer controlled_buffer_1
  \块交换状态机  \u_块交换状态机_1  (
    .Clk(CLK), .Miss(Miss), .Byte0_Ready(\块交换状态机_1_byte0_ready ), .Byte1_Ready(\块交换状态机_1_byte1_ready ),
    .Byte2_Ready(\块交换状态机_1_byte2_ready ), .Byte3_Ready(\块交换状态机_1_byte3_ready ), .Byte0_Ready_2(BlkDataReady),
    .En(Enable));
  assign ByteAddrOut = \块交换状态机_1_byte1_ready  ? {Addr[15:2], 2'b01} : 16'bz;  // Controlled_Buffer controlled_buffer_2
  assign ByteAddrOut = \块交换状态机_1_byte2_ready  ? {Addr[15:2], 2'b10} : 16'bz;  // Controlled_Buffer controlled_buffer_3
  assign ByteAddrOut = \块交换状态机_1_byte3_ready  ? {Addr[15:2], 2'b11} : 16'bz;  // Controlled_Buffer controlled_buffer_4
  Register #(.width(8), .trigger("rising"), .Select("low")) register_1 (
    .D(ByteDataIn), .en(\块交换状态机_1_byte0_ready ), .Q(register_1_q), .clk(CLK));  // open: clr
  Register #(.width(8), .trigger("rising"), .Select("low")) register_2 (
    .D(ByteDataIn), .en(\块交换状态机_1_byte1_ready ), .Q(register_2_q), .clk(CLK));  // open: clr
  Register #(.width(8), .trigger("rising"), .Select("low")) register_3 (
    .D(ByteDataIn), .en(\块交换状态机_1_byte2_ready ), .Q(register_3_q), .clk(CLK));  // open: clr
  Register #(.width(8), .trigger("rising"), .Select("low")) register_4 (
    .D(ByteDataIn), .en(\块交换状态机_1_byte3_ready ), .Q(register_4_q), .clk(CLK));  // open: clr
  assign BlockDataIn = BlkDataReady ? {register_4_q, register_3_q, register_2_q, register_1_q} : 32'bz;  // Controlled_Buffer controlled_buffer_5

  // Notes on the sheet:
  //   数据缓存寄存器
endmodule

// 状态机
module \块交换状态机  (
  input  En,
  input  Clk,
  input  Miss,
  output Byte0_Ready,
  output Byte1_Ready,
  output Byte2_Ready,
  output Byte3_Ready,
  output Byte0_Ready_2
);

  wire and_1_out, and_2_out, and_3_out, and_4_out, and_5_out, and_6_out, and_7_out, Next_Q0, Next_Q1,
       Next_Q2, Next_Q3, not_1_out, not_2_out, not_3_out, not_4_out, not_5_out, not_6_out, not_7_out,
       not_8_out, not_9_out, not_10_out, not_11_out, not_12_out, not_13_out, or_1_out, or_2_out, Q0, Q1, Q2,
       Q3;

  not not_1 (not_1_out, Q3);
  not not_2 (not_2_out, Q3);
  not not_3 (not_3_out, Q2);
  not not_4 (not_4_out, Q3);
  not not_5 (not_5_out, Q1);
  not not_6 (not_6_out, Q3);
  not not_7 (not_7_out, Q0);
  not not_8 (not_8_out, Q3);
  not not_9 (not_9_out, Q0);
  D_Flip_Flop #(.trigger("rising"), .Pre_Clr_Positions("LEGACY"), .NegatePresetClear("false"), .enable("true"), .NewFFLayout("false")) d_ff_1 (
    .clk(Clk), .D(Next_Q3), .Q(Q3), .en(En));  // open: Qn, preset, reset
  D_Flip_Flop #(.trigger("rising"), .Pre_Clr_Positions("LEGACY"), .NegatePresetClear("false"), .enable("true"), .NewFFLayout("false")) d_ff_2 (
    .clk(Clk), .D(Next_Q2), .Q(Q2), .en(En));  // open: Qn, preset, reset
  D_Flip_Flop #(.trigger("rising"), .Pre_Clr_Positions("LEGACY"), .NegatePresetClear("false"), .enable("true"), .NewFFLayout("false")) d_ff_3 (
    .clk(Clk), .D(Next_Q1), .Q(Q1), .en(En));  // open: Qn, preset, reset
  D_Flip_Flop #(.trigger("rising"), .Pre_Clr_Positions("LEGACY"), .NegatePresetClear("false"), .enable("true"), .NewFFLayout("false")) d_ff_4 (
    .clk(Clk), .D(Next_Q0), .Q(Q0), .en(En));  // open: Qn, preset, reset
  and and_1 (and_1_out, not_1_out, Q2, Q1, Q0);
  and and_2 (and_2_out, not_2_out, not_3_out, Q1, Q0);
  not not_10 (not_10_out, Q3);
  and and_3 (and_3_out, not_10_out, Q2, not_11_out);
  not not_11 (not_11_out, Q1);
  not not_12 (not_12_out, Q3);
  and and_4 (and_4_out, not_12_out, Q2, not_13_out);
  not not_13 (not_13_out, Q0);
  and and_5 (and_5_out, not_4_out, not_5_out, Q0);
  and and_6 (and_6_out, not_6_out, Q1, not_7_out);
  and and_7 (and_7_out, not_8_out, not_9_out);
  or or_1 (or_1_out, and_2_out, and_3_out, and_4_out);
  or or_2 (or_2_out, and_5_out, and_6_out);
  Decoder #(.select(4), .tristate("false"), .disabled(0), .enable("false")) decoder_1 (
    .out1(Byte0_Ready), .out3(Byte1_Ready), .out5(Byte2_Ready), .out7(Byte3_Ready), .out8(Byte0_Ready_2),
    .sel({Q3, Q2, Q1, Q0}));  // open: out0, out2, out4, out6, out9, out10, out11, out12, out13, out14, out15
  and and_8 (Next_Q3, and_1_out, Miss);
  and and_9 (Next_Q2, or_1_out, Miss);
  and and_10 (Next_Q1, Miss, or_2_out);
  and and_11 (Next_Q0, Miss, and_7_out);
endmodule
